// Logisim project Processador - Ana Luiza, Beatriz Moggio, Felipe Evangelista, Isabela Barotto.circ as structural Verilog: 8 circuits, main circuit main
module main (
  input  [10:0] \Memória ,
  input  R_W,
  output [7:0] \Saída 
);

  wire CLK;
  wire [2:0] \memória_8x11_1_out_4_2 ;
  wire [3:0] contador_1_out_2;
  wire [7:0] \memória_8x11_1_out_4 , ula_8_ops_1_out_4;

  contador contador_1 (.in_1(CLK), .out_2(contador_1_out_2));
  Clock clock_1 (.out(CLK));
  // Probe on contador_1_out_2
  // Probe on \memória_8x11_1_out_4 
  // Probe on \memória_8x11_1_out_4_2 
  // Probe on \memória_8x11_1_out_4_2 
  \memória__8x11  \memória_8x11_1  (
    .in_1(contador_1_out_2), .R_W(R_W), .Input(\Memória ),
    .out_4({\memória_8x11_1_out_4_2 , \memória_8x11_1_out_4 }));
  // Probe on ula_8_ops_1_out_4
  ula__8_ops ula_8_ops_1 (
    .in_1(\Saída ), .in_2(\memória_8x11_1_out_4 ), .in_3(\memória_8x11_1_out_4_2 ), .out_4(ula_8_ops_1_out_4));
  // Probe on \Saída 
  acumulador acumulador_1 (.R_W(CLK), .Input(ula_8_ops_1_out_4), .Output(\Saída ));
  // Probe on \Saída 

  // Notes on the sheet:
  //   Memória
  //   Linha Gravada
  //   Operação
  //   ULA
  //   Entrada
  //   Acumulador
  //   Operações:
  //   000 - AND
  //   001 - OR
  //   010 - XOR
  //   011 - ADD
  //   100 - SUB
  //   101 - MUL
  //   110 - DIV
  //   111 - MOD
endmodule

module lookahead (
  input  A,
  input  B,
  input  Cin,
  output S
);

  wire xor_1_out;

  xor xor_1 (xor_1_out, B, Cin);
  xor xor_2 (S, A, xor_1_out);
endmodule

module lookahead__8_bits (
  input  [7:0] in_1,
  input  [7:0] in_2,
  input  \SUBTRAÇÃO__1 ,
  output [7:0] out_4
);

  wire and_1_out, and_2_out, and_3_out, and_4_out, and_5_out, and_6_out, and_7_out, and_8_out, and_9_out,
       and_10_out, and_11_out, and_12_out, and_13_out, and_14_out, and_15_out, and_16_out, and_17_out,
       and_18_out, and_19_out, and_20_out, and_21_out, and_22_out, and_23_out, and_24_out, and_25_out,
       and_26_out, and_27_out, and_28_out, C1_out, C2_out, C3_out, C4_out, C5_out, C6_out, C7_out, G0_out,
       G1_out, G2_out, G3_out, G4_out, G5_out, G6_out, P0_out, P1_out, P2_out, P3_out, P4_out, P5_out, P6_out;
  wire [7:0] xor_1_out;

  // Probe on in_1
  // Probe on in_2
  assign xor_1_out = {8{\SUBTRAÇÃO__1 }} ^ in_2;  // XOR_Gate xor_1, 8 bits wide
  // Probe on out_4
  and and_1 (and_1_out, P6_out, G5_out);
  and and_2 (and_2_out, P6_out, P5_out, P4_out, G3_out);
  and and_3 (and_3_out, P6_out, P5_out, G4_out);
  or C7 (C7_out, G6_out, and_1_out, and_3_out, and_2_out, and_4_out, and_5_out, and_6_out, and_7_out);
  and and_4 (and_4_out, P6_out, P5_out, P4_out, P3_out, G2_out);
  and and_5 (and_5_out, P6_out, P5_out, P4_out, P3_out, P2_out, G1_out);
  and and_6 (and_6_out, P6_out, P5_out, P4_out, P3_out, P2_out, P1_out, G0_out);
  and and_7 (and_7_out, P6_out, P5_out, P4_out, P3_out, P2_out, P1_out, and_28_out);
  lookahead lookahead_1 (.A(C7_out), .B(in_1[7]), .Cin(xor_1_out[7]), .S(out_4[7]));
  and and_8 (and_8_out, P5_out, P4_out, G3_out);
  and and_9 (and_9_out, P5_out, G4_out);
  or C6 (C6_out, G5_out, and_9_out, and_8_out, and_11_out, and_10_out, and_12_out, and_13_out);
  and and_10 (and_10_out, P5_out, P4_out, P3_out, P2_out, G1_out);
  and and_11 (and_11_out, P5_out, P4_out, P3_out, G2_out);
  and and_12 (and_12_out, P5_out, P4_out, P3_out, P2_out, P1_out, G0_out);
  and and_13 (and_13_out, P5_out, P4_out, P3_out, P2_out, P1_out, and_28_out);
  lookahead lookahead_2 (.A(C6_out), .B(in_1[6]), .Cin(xor_1_out[6]), .S(out_4[6]));
  and and_14 (and_14_out, P4_out, P3_out, G2_out);
  and and_15 (and_15_out, P4_out, G3_out);
  or C5 (C5_out, G4_out, and_15_out, and_14_out, and_16_out, and_18_out, and_17_out);
  and and_16 (and_16_out, P4_out, P3_out, P2_out, G1_out);
  and and_17 (and_17_out, P4_out, P3_out, P2_out, P1_out, and_28_out);
  and and_18 (and_18_out, P4_out, P3_out, P2_out, P1_out, G0_out);
  lookahead lookahead_3 (.A(C5_out), .B(in_1[5]), .Cin(xor_1_out[5]), .S(out_4[5]));
  and and_19 (and_19_out, P3_out, P2_out, G1_out);
  and and_20 (and_20_out, P3_out, G2_out);
  or C4 (C4_out, G3_out, and_20_out, and_19_out, and_21_out, and_22_out);
  and and_21 (and_21_out, P3_out, P2_out, P1_out, G0_out);
  and and_22 (and_22_out, P3_out, P2_out, P1_out, and_28_out);
  lookahead lookahead_4 (.A(C4_out), .B(in_1[4]), .Cin(xor_1_out[4]), .S(out_4[4]));
  and and_23 (and_23_out, P2_out, G1_out);
  or C3 (C3_out, G2_out, and_23_out, and_24_out, and_25_out);
  and and_24 (and_24_out, P2_out, P1_out, G0_out);
  and and_25 (and_25_out, P2_out, P1_out, and_28_out);
  lookahead lookahead_5 (.A(C3_out), .B(in_1[3]), .Cin(xor_1_out[3]), .S(out_4[3]));
  and and_26 (and_26_out, P1_out, G0_out);
  or C2 (C2_out, G1_out, and_26_out, and_27_out);
  and and_27 (and_27_out, P1_out, and_28_out);
  lookahead lookahead_6 (.A(C2_out), .B(in_1[2]), .Cin(xor_1_out[2]), .S(out_4[2]));
  or C1 (C1_out, G0_out, and_28_out);
  lookahead lookahead_7 (.A(C1_out), .B(in_1[1]), .Cin(xor_1_out[1]), .S(out_4[1]));
  lookahead lookahead_8 (.A(\SUBTRAÇÃO__1 ), .B(in_1[0]), .Cin(xor_1_out[0]), .S(out_4[0]));
  or P6 (P6_out, in_1[6], xor_1_out[6]);
  or P5 (P5_out, in_1[5], xor_1_out[5]);
  or P4 (P4_out, in_1[4], xor_1_out[4]);
  or P2 (P2_out, in_1[2], xor_1_out[2]);
  or P3 (P3_out, in_1[3], xor_1_out[3]);
  or P1 (P1_out, in_1[1], xor_1_out[1]);
  or P0 (P0_out, in_1[0], xor_1_out[0]);
  and and_28 (and_28_out, P0_out, \SUBTRAÇÃO__1 );
  and G5 (G5_out, in_1[5], xor_1_out[5]);
  and G6 (G6_out, in_1[6], xor_1_out[6]);
  and G4 (G4_out, in_1[4], xor_1_out[4]);
  and G3 (G3_out, in_1[3], xor_1_out[3]);
  and G2 (G2_out, in_1[2], xor_1_out[2]);
  and G1 (G1_out, in_1[1], xor_1_out[1]);
  and G0 (G0_out, in_1[0], xor_1_out[0]);

  // Other names for the same wires on the sheet: op = \SUBTRAÇÃO__1 

  // Notes on the sheet:
  //   SOMA (0)
  //   Resultado
endmodule

module \memória__8x11  (
  input  [3:0] in_1,
  input  [10:0] Input,
  input  R_W,
  output [10:0] out_4
);

  wire and_1_out, and_2_out, and_3_out, and_4_out, and_5_out, and_6_out, and_7_out, and_8_out, and_9_out,
       and_10_out, and_11_out, and_12_out, and_13_out, and_14_out, and_15_out, and_16_out, and_17_out,
       and_18_out, and_19_out, and_20_out, and_21_out, and_22_out, and_23_out, and_24_out, and_25_out,
       and_26_out, and_27_out, and_28_out, and_29_out, and_30_out, and_31_out, and_32_out, and_33_out,
       and_34_out, and_35_out, and_36_out, and_37_out, and_38_out, and_39_out, and_40_out, and_41_out,
       and_42_out, and_43_out, and_44_out, and_45_out, and_46_out, and_47_out, and_48_out, and_49_out,
       and_50_out, and_51_out, and_52_out, and_53_out, and_54_out, and_55_out, and_56_out, and_57_out,
       and_58_out, and_59_out, and_60_out, and_61_out, and_62_out, and_63_out, and_64_out, and_65_out,
       and_66_out, and_67_out, and_68_out, and_69_out, and_70_out, and_71_out, and_72_out, and_73_out,
       and_74_out, and_75_out, and_76_out, and_77_out, and_78_out, and_79_out, and_80_out, and_81_out,
       and_82_out, and_83_out, and_84_out, and_85_out, and_86_out, and_87_out, and_88_out, and_89_out,
       and_90_out, and_91_out, and_92_out, and_93_out, and_94_out, and_95_out, and_96_out, and_97_out,
       and_98_out, and_99_out, and_100_out, and_101_out, and_102_out, and_103_out, and_104_out, d_ff_1_q,
       d_ff_2_q, d_ff_3_q, d_ff_4_q, d_ff_5_q, d_ff_6_q, d_ff_7_q, d_ff_8_q, d_ff_9_q, d_ff_10_q, d_ff_11_q,
       d_ff_12_q, d_ff_13_q, d_ff_14_q, d_ff_15_q, d_ff_16_q, d_ff_17_q, d_ff_18_q, d_ff_19_q, d_ff_20_q,
       d_ff_21_q, d_ff_22_q, d_ff_23_q, d_ff_24_q, d_ff_25_q, d_ff_26_q, d_ff_27_q, d_ff_28_q, d_ff_29_q,
       d_ff_30_q, d_ff_31_q, d_ff_32_q, d_ff_33_q, d_ff_34_q, d_ff_35_q, d_ff_36_q, d_ff_37_q, d_ff_38_q,
       d_ff_39_q, d_ff_40_q, d_ff_41_q, d_ff_42_q, d_ff_43_q, d_ff_44_q, d_ff_45_q, d_ff_46_q, d_ff_47_q,
       d_ff_48_q, d_ff_49_q, d_ff_50_q, d_ff_51_q, d_ff_52_q, d_ff_53_q, d_ff_54_q, d_ff_55_q, d_ff_56_q,
       d_ff_57_q, d_ff_58_q, d_ff_59_q, d_ff_60_q, d_ff_61_q, d_ff_62_q, d_ff_63_q, d_ff_64_q, d_ff_65_q,
       d_ff_66_q, d_ff_67_q, d_ff_68_q, d_ff_69_q, d_ff_70_q, d_ff_71_q, d_ff_72_q, d_ff_73_q, d_ff_74_q,
       d_ff_75_q, d_ff_76_q, d_ff_77_q, d_ff_78_q, d_ff_79_q, d_ff_80_q, d_ff_81_q, d_ff_82_q, d_ff_83_q,
       d_ff_84_q, d_ff_85_q, d_ff_86_q, d_ff_87_q, d_ff_88_q;

  and and_1 (and_1_out, ~in_1[0], ~in_1[1], ~in_1[2]);  // AND_Gate
  and and_2 (and_2_out, in_1[0], ~in_1[1], ~in_1[2]);  // AND_Gate
  and and_3 (and_3_out, ~in_1[0], in_1[1], ~in_1[2]);  // AND_Gate
  and and_4 (and_4_out, in_1[0], in_1[1], ~in_1[2]);  // AND_Gate
  and and_5 (and_5_out, ~in_1[0], ~in_1[1], in_1[2]);  // AND_Gate
  and and_6 (and_6_out, in_1[0], ~in_1[1], in_1[2]);  // AND_Gate
  and and_7 (and_7_out, ~in_1[0], in_1[1], in_1[2]);  // AND_Gate
  and and_8 (and_8_out, in_1[0], in_1[1], in_1[2]);
  and and_9 (and_9_out, and_1_out, R_W);
  and and_10 (and_10_out, and_2_out, R_W);
  and and_11 (and_11_out, and_3_out, R_W);
  and and_12 (and_12_out, and_4_out, R_W);
  and and_13 (and_13_out, and_5_out, R_W);
  and and_14 (and_14_out, and_6_out, R_W);
  and and_15 (and_15_out, and_7_out, R_W);
  and and_16 (and_16_out, and_8_out, R_W);
  D_Flip_Flop d_ff_1 (.clk(and_9_out), .D(Input[10]), .Q(d_ff_1_q));  // open: Qn, preset, en, reset
  and and_17 (and_17_out, d_ff_1_q, and_1_out);
  D_Flip_Flop d_ff_2 (.clk(and_10_out), .D(Input[10]), .Q(d_ff_2_q));  // open: Qn, preset, en, reset
  and and_18 (and_18_out, d_ff_2_q, and_2_out);
  D_Flip_Flop d_ff_3 (.clk(and_11_out), .D(Input[10]), .Q(d_ff_3_q));  // open: Qn, preset, en, reset
  and and_19 (and_19_out, d_ff_3_q, and_3_out);
  D_Flip_Flop d_ff_4 (.clk(and_12_out), .D(Input[10]), .Q(d_ff_4_q));  // open: Qn, preset, en, reset
  and and_20 (and_20_out, d_ff_4_q, and_4_out);
  D_Flip_Flop d_ff_5 (.clk(and_13_out), .D(Input[10]), .Q(d_ff_5_q));  // open: Qn, preset, en, reset
  and and_21 (and_21_out, d_ff_5_q, and_5_out);
  D_Flip_Flop d_ff_6 (.clk(and_14_out), .D(Input[10]), .Q(d_ff_6_q));  // open: Qn, preset, en, reset
  and and_22 (and_22_out, d_ff_6_q, and_6_out);
  D_Flip_Flop d_ff_7 (.clk(and_15_out), .D(Input[10]), .Q(d_ff_7_q));  // open: Qn, preset, en, reset
  and and_23 (and_23_out, d_ff_7_q, and_7_out);
  D_Flip_Flop d_ff_8 (.clk(and_16_out), .D(Input[10]), .Q(d_ff_8_q));  // open: Qn, preset, en, reset
  and and_24 (and_24_out, d_ff_8_q, and_8_out);
  or or_1 (out_4[10], and_24_out, and_23_out, and_22_out, and_21_out, and_20_out, and_19_out, and_18_out, and_17_out);
  D_Flip_Flop d_ff_9 (.clk(and_9_out), .D(Input[9]), .Q(d_ff_9_q));  // open: Qn, preset, en, reset
  and and_25 (and_25_out, d_ff_9_q, and_1_out);
  D_Flip_Flop d_ff_10 (.clk(and_10_out), .D(Input[9]), .Q(d_ff_10_q));  // open: Qn, preset, en, reset
  and and_26 (and_26_out, d_ff_10_q, and_2_out);
  D_Flip_Flop d_ff_11 (.clk(and_11_out), .D(Input[9]), .Q(d_ff_11_q));  // open: Qn, preset, en, reset
  and and_27 (and_27_out, d_ff_11_q, and_3_out);
  D_Flip_Flop d_ff_12 (.clk(and_12_out), .D(Input[9]), .Q(d_ff_12_q));  // open: Qn, preset, en, reset
  and and_28 (and_28_out, d_ff_12_q, and_4_out);
  D_Flip_Flop d_ff_13 (.clk(and_13_out), .D(Input[9]), .Q(d_ff_13_q));  // open: Qn, preset, en, reset
  and and_29 (and_29_out, d_ff_13_q, and_5_out);
  D_Flip_Flop d_ff_14 (.clk(and_14_out), .D(Input[9]), .Q(d_ff_14_q));  // open: Qn, preset, en, reset
  and and_30 (and_30_out, d_ff_14_q, and_6_out);
  D_Flip_Flop d_ff_15 (.clk(and_15_out), .D(Input[9]), .Q(d_ff_15_q));  // open: Qn, preset, en, reset
  and and_31 (and_31_out, d_ff_15_q, and_7_out);
  D_Flip_Flop d_ff_16 (.clk(and_16_out), .D(Input[9]), .Q(d_ff_16_q));  // open: Qn, preset, en, reset
  and and_32 (and_32_out, d_ff_16_q, and_8_out);
  or or_2 (out_4[9], and_32_out, and_31_out, and_30_out, and_29_out, and_28_out, and_27_out, and_26_out, and_25_out);
  D_Flip_Flop d_ff_17 (.clk(and_9_out), .D(Input[8]), .Q(d_ff_17_q));  // open: Qn, preset, en, reset
  D_Flip_Flop d_ff_18 (.clk(and_10_out), .D(Input[8]), .Q(d_ff_18_q));  // open: Qn, preset, en, reset
  D_Flip_Flop d_ff_19 (.clk(and_11_out), .D(Input[8]), .Q(d_ff_19_q));  // open: Qn, preset, en, reset
  D_Flip_Flop d_ff_20 (.clk(and_12_out), .D(Input[8]), .Q(d_ff_20_q));  // open: Qn, preset, en, reset
  D_Flip_Flop d_ff_21 (.clk(and_13_out), .D(Input[8]), .Q(d_ff_21_q));  // open: Qn, preset, en, reset
  D_Flip_Flop d_ff_22 (.clk(and_14_out), .D(Input[8]), .Q(d_ff_22_q));  // open: Qn, preset, en, reset
  D_Flip_Flop d_ff_23 (.clk(and_15_out), .D(Input[8]), .Q(d_ff_23_q));  // open: Qn, preset, en, reset
  D_Flip_Flop d_ff_24 (.clk(and_16_out), .D(Input[8]), .Q(d_ff_24_q));  // open: Qn, preset, en, reset
  and and_33 (and_33_out, d_ff_17_q, and_1_out);
  and and_34 (and_34_out, d_ff_18_q, and_2_out);
  and and_35 (and_35_out, d_ff_19_q, and_3_out);
  and and_36 (and_36_out, d_ff_20_q, and_4_out);
  and and_37 (and_37_out, d_ff_21_q, and_5_out);
  and and_38 (and_38_out, d_ff_22_q, and_6_out);
  and and_39 (and_39_out, d_ff_23_q, and_7_out);
  and and_40 (and_40_out, d_ff_24_q, and_8_out);
  or or_3 (out_4[8], and_40_out, and_39_out, and_38_out, and_37_out, and_36_out, and_35_out, and_34_out, and_33_out);
  D_Flip_Flop d_ff_25 (.clk(and_9_out), .D(Input[7]), .Q(d_ff_25_q));  // open: Qn, preset, en, reset
  and and_41 (and_41_out, d_ff_25_q, and_1_out);
  D_Flip_Flop d_ff_26 (.clk(and_10_out), .D(Input[7]), .Q(d_ff_26_q));  // open: Qn, preset, en, reset
  and and_42 (and_42_out, d_ff_26_q, and_2_out);
  D_Flip_Flop d_ff_27 (.clk(and_11_out), .D(Input[7]), .Q(d_ff_27_q));  // open: Qn, preset, en, reset
  and and_43 (and_43_out, d_ff_27_q, and_3_out);
  D_Flip_Flop d_ff_28 (.clk(and_12_out), .D(Input[7]), .Q(d_ff_28_q));  // open: Qn, preset, en, reset
  and and_44 (and_44_out, d_ff_28_q, and_4_out);
  D_Flip_Flop d_ff_29 (.clk(and_13_out), .D(Input[7]), .Q(d_ff_29_q));  // open: Qn, preset, en, reset
  and and_45 (and_45_out, d_ff_29_q, and_5_out);
  D_Flip_Flop d_ff_30 (.clk(and_14_out), .D(Input[7]), .Q(d_ff_30_q));  // open: Qn, preset, en, reset
  and and_46 (and_46_out, d_ff_30_q, and_6_out);
  D_Flip_Flop d_ff_31 (.clk(and_15_out), .D(Input[7]), .Q(d_ff_31_q));  // open: Qn, preset, en, reset
  and and_47 (and_47_out, d_ff_31_q, and_7_out);
  D_Flip_Flop d_ff_32 (.clk(and_16_out), .D(Input[7]), .Q(d_ff_32_q));  // open: Qn, preset, en, reset
  and and_48 (and_48_out, d_ff_32_q, and_8_out);
  or or_4 (out_4[7], and_48_out, and_47_out, and_46_out, and_45_out, and_44_out, and_43_out, and_42_out, and_41_out);
  D_Flip_Flop d_ff_33 (.clk(and_9_out), .D(Input[6]), .Q(d_ff_33_q));  // open: Qn, preset, en, reset
  D_Flip_Flop d_ff_34 (.clk(and_10_out), .D(Input[6]), .Q(d_ff_34_q));  // open: Qn, preset, en, reset
  D_Flip_Flop d_ff_35 (.clk(and_11_out), .D(Input[6]), .Q(d_ff_35_q));  // open: Qn, preset, en, reset
  D_Flip_Flop d_ff_36 (.clk(and_12_out), .D(Input[6]), .Q(d_ff_36_q));  // open: Qn, preset, en, reset
  D_Flip_Flop d_ff_37 (.clk(and_13_out), .D(Input[6]), .Q(d_ff_37_q));  // open: Qn, preset, en, reset
  D_Flip_Flop d_ff_38 (.clk(and_14_out), .D(Input[6]), .Q(d_ff_38_q));  // open: Qn, preset, en, reset
  D_Flip_Flop d_ff_39 (.clk(and_15_out), .D(Input[6]), .Q(d_ff_39_q));  // open: Qn, preset, en, reset
  D_Flip_Flop d_ff_40 (.clk(and_16_out), .D(Input[6]), .Q(d_ff_40_q));  // open: Qn, preset, en, reset
  and and_49 (and_49_out, d_ff_33_q, and_1_out);
  and and_50 (and_50_out, d_ff_34_q, and_2_out);
  and and_51 (and_51_out, d_ff_35_q, and_3_out);
  and and_52 (and_52_out, d_ff_36_q, and_4_out);
  and and_53 (and_53_out, d_ff_37_q, and_5_out);
  and and_54 (and_54_out, d_ff_38_q, and_6_out);
  and and_55 (and_55_out, d_ff_39_q, and_7_out);
  and and_56 (and_56_out, d_ff_40_q, and_8_out);
  or or_5 (out_4[6], and_56_out, and_55_out, and_54_out, and_53_out, and_52_out, and_51_out, and_50_out, and_49_out);
  D_Flip_Flop d_ff_41 (.clk(and_9_out), .D(Input[5]), .Q(d_ff_41_q));  // open: Qn, preset, en, reset
  and and_57 (and_57_out, d_ff_41_q, and_1_out);
  D_Flip_Flop d_ff_42 (.clk(and_10_out), .D(Input[5]), .Q(d_ff_42_q));  // open: Qn, preset, en, reset
  and and_58 (and_58_out, d_ff_42_q, and_2_out);
  D_Flip_Flop d_ff_43 (.clk(and_11_out), .D(Input[5]), .Q(d_ff_43_q));  // open: Qn, preset, en, reset
  and and_59 (and_59_out, d_ff_43_q, and_3_out);
  D_Flip_Flop d_ff_44 (.clk(and_12_out), .D(Input[5]), .Q(d_ff_44_q));  // open: Qn, preset, en, reset
  and and_60 (and_60_out, d_ff_44_q, and_4_out);
  D_Flip_Flop d_ff_45 (.clk(and_13_out), .D(Input[5]), .Q(d_ff_45_q));  // open: Qn, preset, en, reset
  and and_61 (and_61_out, d_ff_45_q, and_5_out);
  D_Flip_Flop d_ff_46 (.clk(and_14_out), .D(Input[5]), .Q(d_ff_46_q));  // open: Qn, preset, en, reset
  and and_62 (and_62_out, d_ff_46_q, and_6_out);
  D_Flip_Flop d_ff_47 (.clk(and_15_out), .D(Input[5]), .Q(d_ff_47_q));  // open: Qn, preset, en, reset
  and and_63 (and_63_out, d_ff_47_q, and_7_out);
  D_Flip_Flop d_ff_48 (.clk(and_16_out), .D(Input[5]), .Q(d_ff_48_q));  // open: Qn, preset, en, reset
  and and_64 (and_64_out, d_ff_48_q, and_8_out);
  or or_6 (out_4[5], and_64_out, and_63_out, and_62_out, and_61_out, and_60_out, and_59_out, and_58_out, and_57_out);
  D_Flip_Flop d_ff_49 (.clk(and_9_out), .D(Input[4]), .Q(d_ff_49_q));  // open: Qn, preset, en, reset
  and and_65 (and_65_out, d_ff_49_q, and_1_out);
  D_Flip_Flop d_ff_50 (.clk(and_10_out), .D(Input[4]), .Q(d_ff_50_q));  // open: Qn, preset, en, reset
  and and_66 (and_66_out, d_ff_50_q, and_2_out);
  D_Flip_Flop d_ff_51 (.clk(and_11_out), .D(Input[4]), .Q(d_ff_51_q));  // open: Qn, preset, en, reset
  and and_67 (and_67_out, d_ff_51_q, and_3_out);
  D_Flip_Flop d_ff_52 (.clk(and_12_out), .D(Input[4]), .Q(d_ff_52_q));  // open: Qn, preset, en, reset
  and and_68 (and_68_out, d_ff_52_q, and_4_out);
  D_Flip_Flop d_ff_53 (.clk(and_13_out), .D(Input[4]), .Q(d_ff_53_q));  // open: Qn, preset, en, reset
  and and_69 (and_69_out, d_ff_53_q, and_5_out);
  D_Flip_Flop d_ff_54 (.clk(and_14_out), .D(Input[4]), .Q(d_ff_54_q));  // open: Qn, preset, en, reset
  and and_70 (and_70_out, d_ff_54_q, and_6_out);
  D_Flip_Flop d_ff_55 (.clk(and_15_out), .D(Input[4]), .Q(d_ff_55_q));  // open: Qn, preset, en, reset
  and and_71 (and_71_out, d_ff_55_q, and_7_out);
  D_Flip_Flop d_ff_56 (.clk(and_16_out), .D(Input[4]), .Q(d_ff_56_q));  // open: Qn, preset, en, reset
  and and_72 (and_72_out, d_ff_56_q, and_8_out);
  or or_7 (out_4[4], and_72_out, and_71_out, and_70_out, and_69_out, and_68_out, and_67_out, and_66_out, and_65_out);
  D_Flip_Flop d_ff_57 (.clk(and_9_out), .D(Input[3]), .Q(d_ff_57_q));  // open: Qn, preset, en, reset
  D_Flip_Flop d_ff_58 (.clk(and_10_out), .D(Input[3]), .Q(d_ff_58_q));  // open: Qn, preset, en, reset
  D_Flip_Flop d_ff_59 (.clk(and_11_out), .D(Input[3]), .Q(d_ff_59_q));  // open: Qn, preset, en, reset
  D_Flip_Flop d_ff_60 (.clk(and_12_out), .D(Input[3]), .Q(d_ff_60_q));  // open: Qn, preset, en, reset
  D_Flip_Flop d_ff_61 (.clk(and_13_out), .D(Input[3]), .Q(d_ff_61_q));  // open: Qn, preset, en, reset
  D_Flip_Flop d_ff_62 (.clk(and_14_out), .D(Input[3]), .Q(d_ff_62_q));  // open: Qn, preset, en, reset
  D_Flip_Flop d_ff_63 (.clk(and_15_out), .D(Input[3]), .Q(d_ff_63_q));  // open: Qn, preset, en, reset
  D_Flip_Flop d_ff_64 (.clk(and_16_out), .D(Input[3]), .Q(d_ff_64_q));  // open: Qn, preset, en, reset
  and and_73 (and_73_out, d_ff_57_q, and_1_out);
  and and_74 (and_74_out, d_ff_58_q, and_2_out);
  and and_75 (and_75_out, d_ff_59_q, and_3_out);
  and and_76 (and_76_out, d_ff_60_q, and_4_out);
  and and_77 (and_77_out, d_ff_61_q, and_5_out);
  and and_78 (and_78_out, d_ff_62_q, and_6_out);
  and and_79 (and_79_out, d_ff_63_q, and_7_out);
  and and_80 (and_80_out, d_ff_64_q, and_8_out);
  or or_8 (out_4[3], and_80_out, and_79_out, and_78_out, and_77_out, and_76_out, and_75_out, and_74_out, and_73_out);
  D_Flip_Flop d_ff_65 (.clk(and_9_out), .D(Input[2]), .Q(d_ff_65_q));  // open: Qn, preset, en, reset
  and and_81 (and_81_out, d_ff_65_q, and_1_out);
  D_Flip_Flop d_ff_66 (.clk(and_10_out), .D(Input[2]), .Q(d_ff_66_q));  // open: Qn, preset, en, reset
  and and_82 (and_82_out, d_ff_66_q, and_2_out);
  D_Flip_Flop d_ff_67 (.clk(and_11_out), .D(Input[2]), .Q(d_ff_67_q));  // open: Qn, preset, en, reset
  and and_83 (and_83_out, d_ff_67_q, and_3_out);
  D_Flip_Flop d_ff_68 (.clk(and_12_out), .D(Input[2]), .Q(d_ff_68_q));  // open: Qn, preset, en, reset
  and and_84 (and_84_out, d_ff_68_q, and_4_out);
  D_Flip_Flop d_ff_69 (.clk(and_13_out), .D(Input[2]), .Q(d_ff_69_q));  // open: Qn, preset, en, reset
  and and_85 (and_85_out, d_ff_69_q, and_5_out);
  D_Flip_Flop d_ff_70 (.clk(and_14_out), .D(Input[2]), .Q(d_ff_70_q));  // open: Qn, preset, en, reset
  and and_86 (and_86_out, d_ff_70_q, and_6_out);
  D_Flip_Flop d_ff_71 (.clk(and_15_out), .D(Input[2]), .Q(d_ff_71_q));  // open: Qn, preset, en, reset
  and and_87 (and_87_out, d_ff_71_q, and_7_out);
  D_Flip_Flop d_ff_72 (.clk(and_16_out), .D(Input[2]), .Q(d_ff_72_q));  // open: Qn, preset, en, reset
  and and_88 (and_88_out, d_ff_72_q, and_8_out);
  or or_9 (out_4[2], and_88_out, and_87_out, and_86_out, and_85_out, and_84_out, and_83_out, and_82_out, and_81_out);
  D_Flip_Flop d_ff_73 (.clk(and_9_out), .D(Input[1]), .Q(d_ff_73_q));  // open: Qn, preset, en, reset
  and and_89 (and_89_out, d_ff_73_q, and_1_out);
  D_Flip_Flop d_ff_74 (.clk(and_10_out), .D(Input[1]), .Q(d_ff_74_q));  // open: Qn, preset, en, reset
  and and_90 (and_90_out, d_ff_74_q, and_2_out);
  D_Flip_Flop d_ff_75 (.clk(and_11_out), .D(Input[1]), .Q(d_ff_75_q));  // open: Qn, preset, en, reset
  and and_91 (and_91_out, d_ff_75_q, and_3_out);
  D_Flip_Flop d_ff_76 (.clk(and_12_out), .D(Input[1]), .Q(d_ff_76_q));  // open: Qn, preset, en, reset
  and and_92 (and_92_out, d_ff_76_q, and_4_out);
  D_Flip_Flop d_ff_77 (.clk(and_13_out), .D(Input[1]), .Q(d_ff_77_q));  // open: Qn, preset, en, reset
  and and_93 (and_93_out, d_ff_77_q, and_5_out);
  D_Flip_Flop d_ff_78 (.clk(and_14_out), .D(Input[1]), .Q(d_ff_78_q));  // open: Qn, preset, en, reset
  and and_94 (and_94_out, d_ff_78_q, and_6_out);
  D_Flip_Flop d_ff_79 (.clk(and_15_out), .D(Input[1]), .Q(d_ff_79_q));  // open: Qn, preset, en, reset
  and and_95 (and_95_out, d_ff_79_q, and_7_out);
  D_Flip_Flop d_ff_80 (.clk(and_16_out), .D(Input[1]), .Q(d_ff_80_q));  // open: Qn, preset, en, reset
  and and_96 (and_96_out, d_ff_80_q, and_8_out);
  or or_10 (out_4[1], and_96_out, and_95_out, and_94_out, and_93_out, and_92_out, and_91_out, and_90_out, and_89_out);
  D_Flip_Flop d_ff_81 (.clk(and_9_out), .D(Input[0]), .Q(d_ff_81_q));  // open: Qn, preset, en, reset
  D_Flip_Flop d_ff_82 (.clk(and_10_out), .D(Input[0]), .Q(d_ff_82_q));  // open: Qn, preset, en, reset
  D_Flip_Flop d_ff_83 (.clk(and_11_out), .D(Input[0]), .Q(d_ff_83_q));  // open: Qn, preset, en, reset
  D_Flip_Flop d_ff_84 (.clk(and_12_out), .D(Input[0]), .Q(d_ff_84_q));  // open: Qn, preset, en, reset
  D_Flip_Flop d_ff_85 (.clk(and_13_out), .D(Input[0]), .Q(d_ff_85_q));  // open: Qn, preset, en, reset
  D_Flip_Flop d_ff_86 (.clk(and_14_out), .D(Input[0]), .Q(d_ff_86_q));  // open: Qn, preset, en, reset
  D_Flip_Flop d_ff_87 (.clk(and_15_out), .D(Input[0]), .Q(d_ff_87_q));  // open: Qn, preset, en, reset
  D_Flip_Flop d_ff_88 (.clk(and_16_out), .D(Input[0]), .Q(d_ff_88_q));  // open: Qn, preset, en, reset
  and and_97 (and_97_out, d_ff_81_q, and_1_out);
  and and_98 (and_98_out, d_ff_82_q, and_2_out);
  and and_99 (and_99_out, d_ff_83_q, and_3_out);
  and and_100 (and_100_out, d_ff_84_q, and_4_out);
  and and_101 (and_101_out, d_ff_85_q, and_5_out);
  and and_102 (and_102_out, d_ff_86_q, and_6_out);
  and and_103 (and_103_out, d_ff_87_q, and_7_out);
  and and_104 (and_104_out, d_ff_88_q, and_8_out);
  or or_11 (out_4[0], and_104_out, and_103_out, and_102_out, and_101_out, and_100_out, and_99_out, and_98_out, and_97_out);
  // also tied to GND on the sheet: in_1[3]

  // Other names for the same wires on the sheet: E0 = Input[0]; E1 = Input[1]; E2 = Input[2]; E3 = Input[3];
  //   E4 = Input[4]; E5 = Input[5]; E6 = Input[6]; E7 = Input[7]; E8 = Input[8]; E9 = Input[9]; E10 = Input[10];
  //   S0 = out_4[0]; S1 = out_4[1]; S2 = out_4[2]; S3 = out_4[3]; S4 = out_4[4]; S5 = out_4[5]; S6 = out_4[6];
  //   S7 = out_4[7]; S8 = out_4[8]; S9 = out_4[9]; S10 = out_4[10]

  // Notes on the sheet:
  //   Output
endmodule

module distribuidor (
  input  in_1,
  output [7:0] out_2
);


  assign out_2 = {8{in_1}};
endmodule

module ula__8_ops (
  input  [7:0] in_1,
  input  [7:0] in_2,
  input  [2:0] in_3,
  output [7:0] out_4
);

  wire and_1_out, and_2_out, and_3_out, and_4_out, and_5_out, and_6_out, and_7_out, and_8_out;
  wire [7:0] and_9_out, and_10_out, and_11_out, and_12_out, and_13_out, and_14_out, and_15_out, and_16_out,
       and_17_out, distribuidor_1_out_2, distribuidor_2_out_2, distribuidor_3_out_2, distribuidor_4_out_2,
       distribuidor_5_out_2, distribuidor_6_out_2, distribuidor_7_out_2, distribuidor_8_out_2, divider_1_out,
       divider_1_rem, lookahead_8_bits_1_out_4, multiplier_1_out, or_1_out, xor_1_out;

  // Probe on in_1
  // Probe on in_2
  // Probe on in_3
  and and_1 (and_1_out, ~in_3[0], ~in_3[1], ~in_3[2]);  // AND_Gate
  and and_2 (and_2_out, in_3[0], ~in_3[1], ~in_3[2]);  // AND_Gate
  and and_3 (and_3_out, ~in_3[0], in_3[1], ~in_3[2]);  // AND_Gate
  and and_4 (and_4_out, in_3[0], in_3[1], ~in_3[2]);  // AND_Gate
  and and_5 (and_5_out, ~in_3[0], ~in_3[1], in_3[2]);  // AND_Gate
  and and_6 (and_6_out, in_3[0], ~in_3[1], in_3[2]);  // AND_Gate
  and and_7 (and_7_out, ~in_3[0], in_3[1], in_3[2]);  // AND_Gate
  and and_8 (and_8_out, in_3[0], in_3[1], in_3[2]);
  lookahead__8_bits lookahead_8_bits_1 (
    .in_1(in_1), .in_2(in_2), .out_4(lookahead_8_bits_1_out_4), .\SUBTRAÇÃO__1 (and_5_out));
  distribuidor distribuidor_1 (.in_1(and_1_out), .out_2(distribuidor_1_out_2));
  distribuidor distribuidor_2 (.in_1(and_2_out), .out_2(distribuidor_2_out_2));
  distribuidor distribuidor_3 (.in_1(and_3_out), .out_2(distribuidor_3_out_2));
  distribuidor distribuidor_4 (.in_1(and_4_out), .out_2(distribuidor_4_out_2));
  distribuidor distribuidor_5 (.in_1(and_5_out), .out_2(distribuidor_5_out_2));
  distribuidor distribuidor_6 (.in_1(and_6_out), .out_2(distribuidor_6_out_2));
  distribuidor distribuidor_7 (.in_1(and_7_out), .out_2(distribuidor_7_out_2));
  distribuidor distribuidor_8 (.in_1(and_8_out), .out_2(distribuidor_8_out_2));
  assign and_9_out = in_1 & in_2;  // AND_Gate and_9, 8 bits wide
  assign or_1_out = in_1 | in_2;  // OR_Gate or_1, 8 bits wide
  assign xor_1_out = in_1 ^ in_2;  // XOR_Gate xor_1, 8 bits wide
  Multiplier multiplier_1 (.a(in_1), .b(in_2), .out(multiplier_1_out));  // open: cin, cout
  Divider divider_1 (.a(in_1), .b(in_2), .out(divider_1_out), .rem(divider_1_rem));  // open: upper
  // Probe on distribuidor_1_out_2
  // Probe on distribuidor_2_out_2
  // Probe on distribuidor_3_out_2
  // Probe on distribuidor_4_out_2
  // Probe on distribuidor_5_out_2
  // Probe on distribuidor_6_out_2
  // Probe on distribuidor_7_out_2
  // Probe on distribuidor_8_out_2
  // Probe on and_10_out
  assign and_10_out = and_9_out & distribuidor_1_out_2;  // AND_Gate and_10, 8 bits wide
  // Probe on and_11_out
  assign and_11_out = or_1_out & distribuidor_2_out_2;  // AND_Gate and_11, 8 bits wide
  // Probe on and_12_out
  assign and_12_out = xor_1_out & distribuidor_3_out_2;  // AND_Gate and_12, 8 bits wide
  // Probe on and_13_out
  assign and_13_out = lookahead_8_bits_1_out_4 & distribuidor_4_out_2;  // AND_Gate and_13, 8 bits wide
  // Probe on and_14_out
  assign and_14_out = lookahead_8_bits_1_out_4 & distribuidor_5_out_2;  // AND_Gate and_14, 8 bits wide
  // Probe on and_15_out
  assign and_15_out = multiplier_1_out & distribuidor_6_out_2;  // AND_Gate and_15, 8 bits wide
  // Probe on and_16_out
  assign and_16_out = divider_1_out & distribuidor_7_out_2;  // AND_Gate and_16, 8 bits wide
  // Probe on and_17_out
  assign and_17_out = divider_1_rem & distribuidor_8_out_2;  // AND_Gate and_17, 8 bits wide
  assign out_4 = and_10_out | and_11_out | and_12_out | and_13_out | and_14_out | and_15_out | and_16_out | and_17_out;  // OR_Gate or_2, 8 bits wide
  // Probe on out_4

  // Notes on the sheet:
  //   AND
  //   OR
  //   XOR
  //   ADD
  //   SUB
  //   MULT
  //   DIV
  //   MOD
endmodule

module acumulador (
  input  [7:0] Input,
  input  R_W,
  output [7:0] Output
);

  D_Flip_Flop d_ff_1 (.clk(R_W), .D(Input[7]), .Q(Output[5]));  // open: Qn, preset, en, reset
  D_Flip_Flop d_ff_2 (.clk(R_W), .D(Input[6]), .Q(Output[6]));  // open: Qn, preset, en, reset
  D_Flip_Flop d_ff_3 (.clk(R_W), .D(Input[5]), .Q(Output[7]));  // open: Qn, preset, en, reset
  D_Flip_Flop d_ff_4 (.clk(R_W), .D(Input[4]), .Q(Output[4]));  // open: Qn, preset, en, reset
  D_Flip_Flop d_ff_5 (.clk(R_W), .D(Input[3]), .Q(Output[3]));  // open: Qn, preset, en, reset
  D_Flip_Flop d_ff_6 (.clk(R_W), .D(Input[2]), .Q(Output[2]));  // open: Qn, preset, en, reset
  D_Flip_Flop d_ff_7 (.clk(R_W), .D(Input[1]), .Q(Output[1]));  // open: Qn, preset, en, reset
  D_Flip_Flop d_ff_8 (.clk(R_W), .D(Input[0]), .Q(Output[0]));  // open: Qn, preset, en, reset

  // Other names for the same wires on the sheet: E0 = Input[0]; E1 = Input[1]; E2 = Input[2]; E3 = Input[3];
  //   E4 = Input[4]; E5 = Input[5]; E6 = Input[6]; E7 = Input[7]; S0 = Output[0]; S1 = Output[1]; S2 = Output[2];
  //   S3 = Output[3]; S4 = Output[4]; S5 = Output[5]; S6 = Output[6]; S7 = Output[7]
endmodule

module contador (
  input  in_1,
  output [3:0] out_2
);

  wire and_1_out;

  Hex_Digit_Display hex_digit_display_1 (.value(out_2));  // open: dp
  and and_1 (and_1_out, ~out_2[0], ~out_2[1], ~out_2[2], out_2[3]);  // AND_Gate
  T_Flip_Flop #(.trigger("falling")) t_ff_1 (
    .clk(in_1), .T(1'b1), .Q(out_2[0]), .reset(and_1_out));  // open: Qn, preset, en
  T_Flip_Flop #(.trigger("falling")) t_ff_2 (
    .clk(out_2[1]), .T(1'b1), .Q(out_2[2]), .reset(and_1_out));  // open: Qn, preset, en
  T_Flip_Flop #(.trigger("falling")) t_ff_3 (
    .clk(out_2[0]), .T(1'b1), .Q(out_2[1]), .reset(and_1_out));  // open: Qn, preset, en
  T_Flip_Flop #(.trigger("falling")) t_ff_4 (
    .clk(out_2[2]), .T(1'b1), .Q(out_2[3]), .reset(and_1_out));  // open: Qn, preset, en
endmodule
