// Logisim project Relogio - Beatriz Moggio (2251604).circ as structural Verilog: 3 circuits, main circuit main
module main (
);

  wire and_1_out, clock_1_out, M_CLK, n7seg_1_a, n7seg_1_b, n7seg_1_c, n7seg_1_d, n7seg_1_e, n7seg_1_f,
       n7seg_1_g, n7seg_2_a, n7seg_2_b, n7seg_2_c, n7seg_2_d, n7seg_2_e, n7seg_2_f, n7seg_2_g, n7seg_3_a,
       n7seg_3_b, n7seg_3_c, n7seg_3_d, n7seg_3_e, n7seg_3_f, n7seg_3_g, n7seg_4_a, n7seg_4_b, n7seg_4_c,
       n7seg_4_d, n7seg_4_e, n7seg_4_f, n7seg_4_g, n7seg_5_a, n7seg_5_b, n7seg_5_c, n7seg_5_d, n7seg_5_e,
       n7seg_5_f, n7seg_5_g, n7seg_6_a, n7seg_6_b, n7seg_6_c, n7seg_6_d, n7seg_6_e, n7seg_6_f, n7seg_6_g,
       S_CLK;
  wire [3:0] H_d, H_u, M_d, M_u, S_d, S_u;
  wire [4:0] t_ff_1_q;
  wire [5:0] t_ff_2_q, t_ff_3_q;

  _7_Segment_Display u_7_segment_display_1 (
    .g(n7seg_2_g), .f(n7seg_2_f), .a(n7seg_2_a), .b(n7seg_2_b), .e(n7seg_2_e), .d(n7seg_2_d), .c(n7seg_2_c));  // open: dp
  _7seg u_7seg_1 (
    .in_1(H_u), .a(n7seg_1_a), .b(n7seg_1_b), .c(n7seg_1_c), .d(n7seg_1_d), .e(n7seg_1_e), .f(n7seg_1_f),
    .g(n7seg_1_g));
  _7seg u_7seg_2 (
    .in_1(H_d), .a(n7seg_2_a), .b(n7seg_2_b), .c(n7seg_2_c), .d(n7seg_2_d), .e(n7seg_2_e), .f(n7seg_2_f),
    .g(n7seg_2_g));
  _7_Segment_Display u_7_segment_display_2 (
    .g(n7seg_1_g), .f(n7seg_1_f), .a(n7seg_1_a), .b(n7seg_1_b), .e(n7seg_1_e), .d(n7seg_1_d), .c(n7seg_1_c));  // open: dp
  _7seg u_7seg_3 (
    .in_1(M_d), .a(n7seg_3_a), .b(n7seg_3_b), .c(n7seg_3_c), .d(n7seg_3_d), .e(n7seg_3_e), .f(n7seg_3_f),
    .g(n7seg_3_g));
  _7_Segment_Display u_7_segment_display_3 (
    .g(n7seg_4_g), .f(n7seg_4_f), .a(n7seg_4_a), .b(n7seg_4_b), .e(n7seg_4_e), .d(n7seg_4_d), .c(n7seg_4_c));  // open: dp
  _7_Segment_Display u_7_segment_display_4 (
    .g(n7seg_3_g), .f(n7seg_3_f), .a(n7seg_3_a), .b(n7seg_3_b), .e(n7seg_3_e), .d(n7seg_3_d), .c(n7seg_3_c));  // open: dp
  _7_Segment_Display u_7_segment_display_5 (
    .g(n7seg_5_g), .f(n7seg_5_f), .a(n7seg_5_a), .b(n7seg_5_b), .e(n7seg_5_e), .d(n7seg_5_d), .c(n7seg_5_c));  // open: dp
  _7seg u_7seg_4 (
    .in_1(M_u), .a(n7seg_4_a), .b(n7seg_4_b), .c(n7seg_4_c), .d(n7seg_4_d), .e(n7seg_4_e), .f(n7seg_4_f),
    .g(n7seg_4_g));
  _7seg u_7seg_5 (
    .in_1(S_d), .a(n7seg_5_a), .b(n7seg_5_b), .c(n7seg_5_c), .d(n7seg_5_d), .e(n7seg_5_e), .f(n7seg_5_f),
    .g(n7seg_5_g));
  _7_Segment_Display u_7_segment_display_6 (
    .g(n7seg_6_g), .f(n7seg_6_f), .a(n7seg_6_a), .b(n7seg_6_b), .e(n7seg_6_e), .d(n7seg_6_d), .c(n7seg_6_c));  // open: dp
  _7seg u_7seg_6 (
    .in_1(S_u), .a(n7seg_6_a), .b(n7seg_6_b), .c(n7seg_6_c), .d(n7seg_6_d), .e(n7seg_6_e), .f(n7seg_6_f),
    .g(n7seg_6_g));
  divisor divisor_1 (.in_1({3'b000, t_ff_1_q}), .DEZENAS(H_d), .UNIDADES(H_u));
  divisor divisor_2 (.in_1({2'b00, t_ff_2_q}), .DEZENAS(M_d), .UNIDADES(M_u));
  divisor divisor_3 (.in_1({2'b00, t_ff_3_q}), .DEZENAS(S_d), .UNIDADES(S_u));
  T_Flip_Flop #(.trigger("falling")) t_ff_1 (
    .clk(M_CLK), .T(1'b1), .Q(t_ff_1_q[0]), .reset(and_1_out));  // open: Qn, preset, en
  and and_1 (and_1_out, ~t_ff_1_q[0], ~t_ff_1_q[1], ~t_ff_1_q[2], t_ff_1_q[3], t_ff_1_q[4]);  // AND_Gate
  T_Flip_Flop #(.trigger("falling")) t_ff_2 (
    .clk(S_CLK), .T(1'b1), .Q(t_ff_2_q[0]), .reset(M_CLK));  // open: Qn, preset, en
  and and_2 (M_CLK, ~t_ff_2_q[0], ~t_ff_2_q[1], t_ff_2_q[2], t_ff_2_q[3], t_ff_2_q[4], t_ff_2_q[5]);  // AND_Gate
  T_Flip_Flop #(.trigger("falling")) t_ff_3 (
    .clk(clock_1_out), .T(1'b1), .Q(t_ff_3_q[0]), .reset(S_CLK));  // open: Qn, preset, en
  Clock #(.highDuration(8), .lowDuration(8)) clock_1 (.out(clock_1_out));
  and and_3 (S_CLK, ~t_ff_3_q[0], ~t_ff_3_q[1], t_ff_3_q[2], t_ff_3_q[3], t_ff_3_q[4], t_ff_3_q[5]);  // AND_Gate
  T_Flip_Flop #(.trigger("falling")) t_ff_4 (
    .clk(t_ff_1_q[0]), .T(1'b1), .Q(t_ff_1_q[1]), .reset(and_1_out));  // open: Qn, preset, en
  T_Flip_Flop #(.trigger("falling")) t_ff_5 (
    .clk(t_ff_2_q[0]), .T(1'b1), .Q(t_ff_2_q[1]), .reset(M_CLK));  // open: Qn, preset, en
  T_Flip_Flop #(.trigger("falling")) t_ff_6 (
    .clk(t_ff_3_q[0]), .T(1'b1), .Q(t_ff_3_q[1]), .reset(S_CLK));  // open: Qn, preset, en
  T_Flip_Flop #(.trigger("falling")) t_ff_7 (
    .clk(t_ff_1_q[1]), .T(1'b1), .Q(t_ff_1_q[2]), .reset(and_1_out));  // open: Qn, preset, en
  T_Flip_Flop #(.trigger("falling")) t_ff_8 (
    .clk(t_ff_2_q[1]), .T(1'b1), .Q(t_ff_2_q[2]), .reset(M_CLK));  // open: Qn, preset, en
  T_Flip_Flop #(.trigger("falling")) t_ff_9 (
    .clk(t_ff_3_q[1]), .T(1'b1), .Q(t_ff_3_q[2]), .reset(S_CLK));  // open: Qn, preset, en
  T_Flip_Flop #(.trigger("falling")) t_ff_10 (
    .clk(t_ff_1_q[2]), .T(1'b1), .Q(t_ff_1_q[3]), .reset(and_1_out));  // open: Qn, preset, en
  T_Flip_Flop #(.trigger("falling")) t_ff_11 (
    .clk(t_ff_2_q[2]), .T(1'b1), .Q(t_ff_2_q[3]), .reset(M_CLK));  // open: Qn, preset, en
  T_Flip_Flop #(.trigger("falling")) t_ff_12 (
    .clk(t_ff_3_q[2]), .T(1'b1), .Q(t_ff_3_q[3]), .reset(S_CLK));  // open: Qn, preset, en
  T_Flip_Flop #(.trigger("falling")) t_ff_13 (
    .clk(t_ff_1_q[3]), .T(1'b1), .Q(t_ff_1_q[4]), .reset(and_1_out));  // open: Qn, preset, en
  T_Flip_Flop #(.trigger("falling")) t_ff_14 (
    .clk(t_ff_2_q[3]), .T(1'b1), .Q(t_ff_2_q[4]), .reset(M_CLK));  // open: Qn, preset, en
  T_Flip_Flop #(.trigger("falling")) t_ff_15 (
    .clk(t_ff_3_q[3]), .T(1'b1), .Q(t_ff_3_q[4]), .reset(S_CLK));  // open: Qn, preset, en
  T_Flip_Flop #(.trigger("falling")) t_ff_16 (
    .clk(t_ff_2_q[4]), .T(1'b1), .Q(t_ff_2_q[5]), .reset(M_CLK));  // open: Qn, preset, en
  T_Flip_Flop #(.trigger("falling")) t_ff_17 (
    .clk(t_ff_3_q[4]), .T(1'b1), .Q(t_ff_3_q[5]), .reset(S_CLK));  // open: Qn, preset, en
endmodule

module divisor (
  input  [7:0] in_1,
  output [3:0] DEZENAS,
  output [3:0] UNIDADES
);

  wire [7:4] divider_1_out, divider_1_rem;

  // Probe on in_1
  Divider divider_1 (
    .a(in_1), .b(8'ha), .out({divider_1_out, DEZENAS}), .rem({divider_1_rem, UNIDADES}));  // open: upper
  // Probe on DEZENAS
  // Probe on UNIDADES
endmodule

module _7seg (
  input  [3:0] in_1,
  output a,
  output b,
  output c,
  output d,
  output e,
  output f,
  output g
);

  wire and_1_out, and_2_out, and_3_out, and_4_out, and_5_out, and_6_out, and_7_out, and_8_out, and_9_out,
       and_10_out, and_11_out, and_12_out, and_13_out, and_14_out, and_15_out, and_16_out, not_1_out,
       not_2_out, not_3_out, not_4_out, not_5_out, not_6_out, not_7_out, not_8_out, not_9_out, not_10_out,
       not_11_out, not_12_out, not_13_out, not_14_out, not_15_out, not_16_out, not_17_out, not_18_out,
       not_19_out, not_20_out, not_21_out;

  // Probe on in_1
  not not_1 (not_1_out, in_1[2]);
  not not_2 (not_2_out, in_1[0]);
  not not_3 (not_3_out, in_1[1]);
  not not_4 (not_4_out, in_1[0]);
  not not_5 (not_5_out, in_1[1]);
  not not_6 (not_6_out, in_1[2]);
  not not_7 (not_7_out, in_1[0]);
  not not_8 (not_8_out, in_1[2]);
  not not_9 (not_9_out, in_1[0]);
  not not_10 (not_10_out, in_1[1]);
  not not_11 (not_11_out, in_1[2]);
  not not_12 (not_12_out, in_1[0]);
  not not_13 (not_13_out, in_1[0]);
  not not_14 (not_14_out, in_1[1]);
  not not_15 (not_15_out, in_1[0]);
  not not_16 (not_16_out, in_1[1]);
  not not_17 (not_17_out, in_1[0]);
  not not_18 (not_18_out, in_1[2]);
  not not_19 (not_19_out, in_1[1]);
  not not_20 (not_20_out, in_1[0]);
  and and_1 (and_1_out, not_1_out, not_2_out);
  and and_2 (and_2_out, in_1[2], in_1[0]);
  not not_21 (not_21_out, in_1[2]);
  and and_3 (and_3_out, not_3_out, not_4_out);
  and and_4 (and_4_out, in_1[1], in_1[0]);
  or or_1 (c, not_5_out, in_1[0], in_1[2]);
  and and_5 (and_5_out, not_6_out, not_7_out);
  and and_6 (and_6_out, not_8_out, in_1[1]);
  and and_7 (and_7_out, in_1[1], not_9_out);
  and and_8 (and_8_out, in_1[2], not_10_out, in_1[0]);
  and and_9 (and_9_out, not_11_out, not_12_out);
  and and_10 (and_10_out, in_1[1], not_13_out);
  and and_11 (and_11_out, not_14_out, not_15_out);
  and and_12 (and_12_out, in_1[2], not_16_out);
  and and_13 (and_13_out, in_1[2], not_17_out);
  and and_14 (and_14_out, not_18_out, in_1[1]);
  and and_15 (and_15_out, in_1[2], not_19_out);
  and and_16 (and_16_out, in_1[2], not_20_out);
  or or_2 (a, and_1_out, in_1[1], and_2_out, in_1[3]);
  or or_3 (b, not_21_out, and_3_out, and_4_out);
  or or_4 (d, and_5_out, and_6_out, and_7_out, and_8_out, in_1[3]);
  or or_5 (e, and_9_out, and_10_out);
  or or_6 (f, and_11_out, and_12_out, and_13_out, in_1[3]);
  or or_7 (g, and_14_out, and_15_out, and_16_out, in_1[3]);
  _7_Segment_Display u_7_segment_display_1 (.g(g), .f(f), .a(a), .b(b), .e(e), .d(d), .c(c));  // open: dp
endmodule
