// Logisim project Somador (8 bits) - Beatriz Moggio (2251604).circ as structural Verilog: 2 circuits, main circuit main
module main (
  input  [7:0] in_1,
  input  [7:0] in_2,
  output [7:0] out_3
);

  wire somador_2_cout, somador_3_cout, somador_4_cout, somador_5_cout, somador_6_cout, somador_7_cout,
       somador_8_cout;

  // Probe on in_1
  // Probe on in_2
  // Probe on out_3
  somador somador_1 (.S(out_3[7]), .A(in_1[7]), .B(in_2[7]), .Cin(somador_2_cout));  // open: Cout
  somador somador_2 (.Cout(somador_2_cout), .S(out_3[6]), .A(in_1[6]), .B(in_2[6]), .Cin(somador_4_cout));
  somador somador_3 (.Cout(somador_3_cout), .S(out_3[4]), .A(in_1[4]), .B(in_2[4]), .Cin(somador_6_cout));
  somador somador_4 (.Cout(somador_4_cout), .S(out_3[5]), .A(in_1[5]), .B(in_2[5]), .Cin(somador_3_cout));
  somador somador_5 (.Cout(somador_5_cout), .S(out_3[2]), .A(in_1[2]), .B(in_2[2]), .Cin(somador_8_cout));
  somador somador_6 (.Cout(somador_6_cout), .S(out_3[3]), .A(in_1[3]), .B(in_2[3]), .Cin(somador_5_cout));
  somador somador_7 (.Cout(somador_7_cout), .S(out_3[0]), .A(in_1[0]), .B(in_2[0]), .Cin(1'b0));
  somador somador_8 (.Cout(somador_8_cout), .S(out_3[1]), .A(in_1[1]), .B(in_2[1]), .Cin(somador_7_cout));
endmodule

module somador (
  input  A,
  input  B,
  input  Cin,
  output Cout,
  output S
);

  wire and_1_out, and_2_out, and_3_out, xor_1_out;

  and and_1 (and_1_out, A, B);
  and and_2 (and_2_out, A, Cin);
  and and_3 (and_3_out, B, Cin);
  xor xor_1 (xor_1_out, B, Cin);
  or or_1 (Cout, and_1_out, and_2_out, and_3_out);
  xor xor_2 (S, xor_1_out, A);
endmodule
