// Logisim project Somador-Subtrator (8 bits) - Beatriz Moggio (2251604).circ as structural Verilog: 2 circuits, main circuit main
module main (
  input  [7:0] in_1,
  input  [7:0] in_2,
  input  in_3,
  output [7:0] out_4
);

  wire somador_1_cout, somador_2_cout, somador_3_cout, somador_4_cout, somador_5_cout, somador_6_cout,
       somador_7_cout, somador_8_cout, xor_2_out;
  wire [7:0] xor_1_out;

  // Probe on in_1
  // Probe on in_2
  assign xor_1_out = {8{in_3}} ^ in_2;  // XOR_Gate xor_1, 8 bits wide
  xor xor_2 (xor_2_out, somador_1_cout, somador_2_cout);
  LED led_1 (.in(xor_2_out));
  // Probe on out_4
  somador somador_1 (.Cout(somador_1_cout), .S(out_4[6]), .A(in_1[6]), .B(xor_1_out[6]), .Cin(somador_4_cout));
  somador somador_2 (.Cout(somador_2_cout), .S(out_4[7]), .A(in_1[7]), .B(xor_1_out[7]), .Cin(somador_1_cout));
  somador somador_3 (.Cout(somador_3_cout), .S(out_4[4]), .A(in_1[4]), .B(xor_1_out[4]), .Cin(somador_5_cout));
  somador somador_4 (.Cout(somador_4_cout), .S(out_4[5]), .A(in_1[5]), .B(xor_1_out[5]), .Cin(somador_3_cout));
  somador somador_5 (.Cout(somador_5_cout), .S(out_4[3]), .A(in_1[3]), .B(xor_1_out[3]), .Cin(somador_6_cout));
  somador somador_6 (.Cout(somador_6_cout), .S(out_4[2]), .A(in_1[2]), .B(xor_1_out[2]), .Cin(somador_7_cout));
  somador somador_7 (.Cout(somador_7_cout), .S(out_4[1]), .A(in_1[1]), .B(xor_1_out[1]), .Cin(somador_8_cout));
  somador somador_8 (.Cout(somador_8_cout), .S(out_4[0]), .A(in_1[0]), .B(xor_1_out[0]), .Cin(in_3));

  // Other names for the same wires on the sheet: op = in_3
endmodule

module somador (
  input  A,
  input  B,
  input  Cin,
  output Cout,
  output S
);

  wire and_1_out, and_2_out, and_3_out, xor_1_out;

  and and_1 (and_1_out, A, B);
  and and_2 (and_2_out, A, Cin);
  and and_3 (and_3_out, B, Cin);
  or or_1 (Cout, and_1_out, and_2_out, and_3_out);
  xor xor_1 (xor_1_out, B, Cin);
  xor xor_2 (S, xor_1_out, A);
endmodule
