// Logisim project Somador-Subtrator Lookahead (8 bits) - Beatriz Moggio (2251604).circ as structural Verilog: 2 circuits, main circuit main
module main (
  input  [7:0] in_1,
  input  [7:0] in_2,
  input  \SUBTRAÇÃO__1 ,
  output [7:0] out_4
);

  wire and_1_out, and_2_out, and_3_out, and_4_out, and_5_out, and_6_out, and_7_out, and_8_out, and_9_out,
       and_10_out, and_11_out, and_12_out, and_13_out, and_14_out, and_15_out, and_16_out, and_17_out,
       and_18_out, and_19_out, and_20_out, and_21_out, and_22_out, and_23_out, and_24_out, and_25_out,
       and_26_out, and_27_out, and_28_out, C1_out, C2_out, C3_out, C4_out, C5_out, C6_out, C7_out, G0_out,
       G1_out, G2_out, G3_out, G4_out, G5_out, G6_out, P0_out, P1_out, P2_out, P3_out, P4_out, P5_out, P6_out;
  wire [7:0] xor_1_out;

  // Probe on in_1
  // Probe on in_2
  assign xor_1_out = {8{\SUBTRAÇÃO__1 }} ^ in_2;  // XOR_Gate xor_1, 8 bits wide
  // Probe on out_4
  and and_1 (and_1_out, P6_out, G5_out);
  and and_2 (and_2_out, P6_out, P5_out, P4_out, G3_out);
  and and_3 (and_3_out, P6_out, P5_out, G4_out);
  or C7 (C7_out, G6_out, and_1_out, and_3_out, and_2_out, and_4_out, and_5_out, and_6_out, and_7_out);
  and and_4 (and_4_out, P6_out, P5_out, P4_out, P3_out, G2_out);
  and and_5 (and_5_out, P6_out, P5_out, P4_out, P3_out, P2_out, G1_out);
  and and_6 (and_6_out, P6_out, P5_out, P4_out, P3_out, P2_out, P1_out, G0_out);
  and and_7 (and_7_out, P6_out, P5_out, P4_out, P3_out, P2_out, P1_out, and_28_out);
  lookahead lookahead_1 (.A(in_1[7]), .B(xor_1_out[7]), .Cin(C7_out), .S(out_4[7]));
  and and_8 (and_8_out, P5_out, P4_out, G3_out);
  and and_9 (and_9_out, P5_out, G4_out);
  or C6 (C6_out, G5_out, and_9_out, and_8_out, and_11_out, and_10_out, and_12_out, and_13_out);
  and and_10 (and_10_out, P5_out, P4_out, P3_out, P2_out, G1_out);
  and and_11 (and_11_out, P5_out, P4_out, P3_out, G2_out);
  and and_12 (and_12_out, P5_out, P4_out, P3_out, P2_out, P1_out, G0_out);
  and and_13 (and_13_out, P5_out, P4_out, P3_out, P2_out, P1_out, and_28_out);
  lookahead lookahead_2 (.A(in_1[6]), .B(xor_1_out[6]), .Cin(C6_out), .S(out_4[6]));
  and and_14 (and_14_out, P4_out, P3_out, G2_out);
  and and_15 (and_15_out, P4_out, G3_out);
  or C5 (C5_out, G4_out, and_15_out, and_14_out, and_16_out, and_18_out, and_17_out);
  and and_16 (and_16_out, P4_out, P3_out, P2_out, G1_out);
  and and_17 (and_17_out, P4_out, P3_out, P2_out, P1_out, and_28_out);
  and and_18 (and_18_out, P4_out, P3_out, P2_out, P1_out, G0_out);
  lookahead lookahead_3 (.A(in_1[5]), .B(xor_1_out[5]), .Cin(C5_out), .S(out_4[5]));
  and and_19 (and_19_out, P3_out, G2_out);
  and and_20 (and_20_out, P3_out, P2_out, G1_out);
  or C4 (C4_out, G3_out, and_19_out, and_20_out, and_21_out, and_22_out);
  and and_21 (and_21_out, P3_out, P2_out, P1_out, G0_out);
  and and_22 (and_22_out, P3_out, P2_out, P1_out, and_28_out);
  lookahead lookahead_4 (.A(in_1[4]), .B(xor_1_out[4]), .Cin(C4_out), .S(out_4[4]));
  and and_23 (and_23_out, P2_out, G1_out);
  or C3 (C3_out, G2_out, and_23_out, and_25_out, and_24_out);
  and and_24 (and_24_out, P2_out, P1_out, and_28_out);
  and and_25 (and_25_out, P2_out, P1_out, G0_out);
  lookahead lookahead_5 (.A(in_1[3]), .B(xor_1_out[3]), .Cin(C3_out), .S(out_4[3]));
  and and_26 (and_26_out, P1_out, G0_out);
  or C2 (C2_out, G1_out, and_26_out, and_27_out);
  and and_27 (and_27_out, P1_out, and_28_out);
  lookahead lookahead_6 (.A(in_1[2]), .B(xor_1_out[2]), .Cin(C2_out), .S(out_4[2]));
  or C1 (C1_out, G0_out, and_28_out);
  lookahead lookahead_7 (.A(in_1[1]), .B(xor_1_out[1]), .Cin(C1_out), .S(out_4[1]));
  lookahead lookahead_8 (.A(in_1[0]), .B(xor_1_out[0]), .Cin(\SUBTRAÇÃO__1 ), .S(out_4[0]));
  or P6 (P6_out, in_1[6], xor_1_out[6]);
  or P4 (P4_out, in_1[4], xor_1_out[4]);
  or P5 (P5_out, in_1[5], xor_1_out[5]);
  or P2 (P2_out, in_1[2], xor_1_out[2]);
  or P3 (P3_out, in_1[3], xor_1_out[3]);
  or P0 (P0_out, in_1[0], xor_1_out[0]);
  or P1 (P1_out, in_1[1], xor_1_out[1]);
  and and_28 (and_28_out, P0_out, \SUBTRAÇÃO__1 );
  and G5 (G5_out, in_1[5], xor_1_out[5]);
  and G6 (G6_out, in_1[6], xor_1_out[6]);
  and G3 (G3_out, in_1[3], xor_1_out[3]);
  and G4 (G4_out, in_1[4], xor_1_out[4]);
  and G1 (G1_out, in_1[1], xor_1_out[1]);
  and G2 (G2_out, in_1[2], xor_1_out[2]);
  and G0 (G0_out, in_1[0], xor_1_out[0]);

  // Other names for the same wires on the sheet: op = \SUBTRAÇÃO__1 

  // Notes on the sheet:
  //   SOMA (0)
  //   Resultado
endmodule

module lookahead (
  input  A,
  input  B,
  input  Cin,
  output S
);

  wire xor_1_out;

  xor xor_1 (xor_1_out, B, Cin);
  xor xor_2 (S, A, xor_1_out);
endmodule
