// Logisim project [T3] Decodificador (Beatriz Moggio, Isabela Barotto).circ as structural Verilog: 1 circuit, main circuit main
module main (
  input  [31:0] \Instrução ,
  output [25:0] ADDR,
  output [15:0] IMM,
  output [5:0] FUNCT,
  output [4:0] SHAMT,
  output [4:0] RD,
  output [4:0] RT,
  output [4:0] RS,
  output [5:0] OPCODE
);


  assign ADDR = \Instrução [25:0];
  assign FUNCT = \Instrução [5:0];
  assign IMM = \Instrução [15:0];
  assign OPCODE = \Instrução [31:26];
  assign RD = \Instrução [15:11];
  assign RS = \Instrução [25:21];
  assign RT = \Instrução [20:16];
  assign SHAMT = \Instrução [10:6];
endmodule
