// Logisim project [T4] Unidade de Controle (Beatriz Moggio, Isabela Barotto).circ as structural Verilog: 1 circuit, main circuit main
module main (
  input  [5:0] OP,
  output ALUScr,
  output RegWrite,
  output RegDest,
  output MemToReg,
  output MemRead,
  output MemWrite,
  output Branch,
  output Jump,
  output [2:0] ALUOp
);

  wire addi, andi, ori, slti;

  and R (RegDest, ~OP[0], ~OP[1], ~OP[2], ~OP[3], ~OP[4], ~OP[5]);  // AND_Gate
  and u_addi (addi, ~OP[0], ~OP[1], ~OP[2], OP[3], ~OP[4], ~OP[5]);  // AND_Gate
  and u_andi (andi, ~OP[0], ~OP[1], OP[2], OP[3], ~OP[4], ~OP[5]);  // AND_Gate
  and u_ori (ori, OP[0], ~OP[1], OP[2], OP[3], ~OP[4], ~OP[5]);  // AND_Gate
  and u_slti (slti, ~OP[0], OP[1], ~OP[2], OP[3], ~OP[4], ~OP[5]);  // AND_Gate
  and lw (MemRead, OP[0], OP[1], ~OP[2], ~OP[3], ~OP[4], OP[5]);  // AND_Gate
  and sw (MemWrite, OP[0], OP[1], ~OP[2], OP[3], ~OP[4], OP[5]);  // AND_Gate
  and beq (Branch, ~OP[0], ~OP[1], OP[2], ~OP[3], ~OP[4], ~OP[5]);  // AND_Gate
  and j (Jump, ~OP[0], OP[1], ~OP[2], ~OP[3], ~OP[4], ~OP[5]);  // AND_Gate
  or or_1 (ALUScr, addi, andi, ori, slti, MemRead, MemWrite);
  or or_2 (RegWrite, RegDest, addi, andi, ori, slti, MemRead);
  or or_3 (ALUOp[0], addi, MemRead, MemWrite, ori, Branch);
  or or_4 (ALUOp[1], andi, ori);
  or or_5 (ALUOp[2], slti, Branch);

  assign MemToReg = MemRead;

  // Other names for the same wires on the sheet: beq = Branch; lw = MemRead; sw = MemWrite

  // Notes on the sheet:
  //   ALUOp
  //   000
  //   001
  //   010
  //   011
  //   100
  //   101
  //   Operação
  //   R
  //   SOMA
  //   AND
  //   OR
  //   SLT
  //   SUB
  //   Instruções
  //   addi, lw, sw
  //   andi
  //   ori
  //   slti
  //   beq
endmodule
