// Logisim project [T5] Datapath e execução.circ as structural Verilog: 11 circuits, main circuit main
module main (
  output out_1
);

  wire ALUSrc, and_1_out, Branch, CL_out, CLK, Jump, MemRead, MemToReg, MemWrite, RegDest, RegWrite, ZERO;
  wire [2:0] ALUOp, OpULA;
  wire [4:0] decodificador_1_rd, decodificador_1_rs, decodificador_1_rt, decodificador_1_shamt,
       multiplexer_3_out;
  wire [5:0] decodificador_1_funct, decodificador_1_opcode;
  wire [15:0] decodificador_1_imm;
  wire [25:0] decodificador_1_addr;
  wire [31:0] A, adder_1_out, adder_2_out, B, imm, inst, memoriadados_1_out_7, multiplexer_1_out,
       multiplexer_2_out, n2_1_out_2, n2conc_1_out_3, pc, ToReg, ula_1_result, WD;

  Adder #(.width(32)) adder_1 (.a(adder_2_out), .b(n2_1_out_2), .out(adder_1_out));  // open: cin, cout
  Adder #(.width(32)) adder_2 (.a(pc), .b(32'h4), .out(adder_2_out));  // open: cin, cout
  Multiplexer #(.width(32)) multiplexer_1 (
    .in0(adder_2_out), .in1(adder_1_out), .out(multiplexer_1_out), .sel(and_1_out));  // open: en
  and and_1 (and_1_out, Branch, ZERO);
  _2conc u_2conc_1 (.out_3(n2conc_1_out_3), .Addr26(decodificador_1_addr), .Pc___4(adder_2_out));
  _2 u_2_1 (.in_1(imm), .out_2(n2_1_out_2));
  Multiplexer #(.width(32)) multiplexer_2 (
    .in0(multiplexer_1_out), .in1(n2conc_1_out_3), .out(multiplexer_2_out), .sel(Jump));  // open: en
  Register #(.width(32)) u_PC (.D(multiplexer_2_out), .Q(pc), .clk(CLK));  // open: en, clr
  MemoriaInstrucoes memoriainstrucoes_1 (.PCADDR(pc), .out_2(inst));
  Decodificador decodificador_1 (
    .ADDR(decodificador_1_addr), .IMM(decodificador_1_imm), .FUNCT(decodificador_1_funct),
    .SHAMT(decodificador_1_shamt), .RD(decodificador_1_rd), .RT(decodificador_1_rt), .RS(decodificador_1_rs),
    .OPCODE(decodificador_1_opcode), .\Instrução (inst));
  UnidadeControle unidadecontrole_1 (
    .OP(decodificador_1_opcode), .ALUOp(ALUOp), .ALUSrc(ALUSrc), .RegWrite(RegWrite), .RegDest(RegDest),
    .MemToReg(MemToReg), .MemRead(MemRead), .MemWrite(MemWrite), .Branch(Branch), .Jump(Jump));
  ExtensorSinal extensorsinal_1 (.IMM16(decodificador_1_imm), .IMM32(imm));
  Multiplexer #(.width(5)) multiplexer_3 (
    .in0(decodificador_1_rt), .in1(decodificador_1_rd), .out(multiplexer_3_out), .sel(RegDest));  // open: en
  ControleULA controleula_1 (.OpULA(OpULA), .FUNCT(decodificador_1_funct), .ALUOp(ALUOp));
  // Probe on pc
  Clock clock_1 (.out(CLK));
  BancoRegistradores bancoregistradores_1 (
    .LR1(decodificador_1_rs), .LR2(decodificador_1_rt), .RW(RegWrite), .LD1(A), .WR(multiplexer_3_out),
    .WD(ToReg), .LD2(WD), .CLK(CLK));
  // Probe on inst
  // Probe on ALUOp
  // Probe on A
  // Probe on OpULA
  Multiplexer #(.width(32)) multiplexer_4 (.in0(WD), .in1(imm), .out(B), .sel(ALUSrc));  // open: en
  // Probe on ToReg
  // Probe on B
  ULA ula_1 (.OP(OpULA), .A(A), .SHAMT(decodificador_1_shamt), .B(B), .ZERO(ZERO), .OVF(out_1), .RESULT(ula_1_result));
  Button CL (.out(CL_out));
  MemoriaDados memoriadados_1 (
    .MemWrite(MemWrite), .\Endereço (ula_1_result), .CLK(CLK), .MemRead(MemRead), .EscreveDado(WD),
    .Clear(CL_out), .out_7(memoriadados_1_out_7));
  Multiplexer #(.width(32)) multiplexer_5 (
    .in0(ula_1_result), .in1(memoriadados_1_out_7), .out(ToReg), .sel(MemToReg));  // open: en
endmodule

module ULA (
  input  [2:0] OP,
  input  [4:0] SHAMT,
  input  [31:0] A,
  input  [31:0] B,
  output ZERO,
  output OVF,
  output [31:0] RESULT
);

  wire ADD_out, and_2_out, and_3_out, and_4_out, and_5_out, bitselector_1_out, bitselector_2_out,
       bitselector_3_out, comparator_1_lt, comparator_2_eq, comparator_3_eq, SUB_out;
  wire [31:0] adder_1_out, and_1_out, bit_extender_1_out, or_1_out, shifter_1_out, shifter_2_out,
       subtractor_1_out;

  // Probe on A
  // Probe on B
  // Probe on RESULT
  Adder #(.width(32)) adder_1 (.a(A), .b(B), .out(adder_1_out));  // open: cin, cout
  Subtractor #(.width(32)) subtractor_1 (.a(A), .b(B), .out(subtractor_1_out));  // open: bin, bout
  assign and_1_out = A & B;  // AND_Gate and_1, 32 bits wide
  assign or_1_out = A | B;  // OR_Gate or_1, 32 bits wide
  Shifter #(.width(32)) shifter_1 (.in(A), .\dist (SHAMT), .out(shifter_1_out));
  Shifter #(.width(32), .shift("lr")) shifter_2 (.in(A), .\dist (SHAMT), .out(shifter_2_out));
  Comparator #(.width(32)) comparator_1 (.a(A), .b(B), .lt(comparator_1_lt));  // open: gt, eq
  assign bit_extender_1_out = {{31{1'b0}}, comparator_1_lt};  // Bit_Extender bit_extender_1
  Multiplexer #(.select(3), .width(32)) multiplexer_1 (
    .in0(adder_1_out), .in1(subtractor_1_out), .in2(and_1_out), .in3(or_1_out), .in4(shifter_1_out),
    .in5(shifter_2_out), .in6(bit_extender_1_out), .out(RESULT), .sel(OP));  // open: in7, en
  BitSelector #(.width(32)) bitselector_1 (.in(A), .out(bitselector_1_out), .sel({5{1'b1}}));
  BitSelector #(.width(32)) bitselector_2 (.in(B), .out(bitselector_2_out), .sel({5{1'b1}}));
  BitSelector #(.width(32)) bitselector_3 (.in(RESULT), .out(bitselector_3_out), .sel({5{1'b1}}));
  Comparator #(.width(1)) comparator_2 (
    .a(bitselector_1_out), .b(bitselector_2_out), .eq(comparator_2_eq));  // open: gt, lt
  and and_2 (and_2_out, comparator_2_eq, ADD_out);
  Comparator #(.width(1)) comparator_3 (
    .a(bitselector_3_out), .b(bitselector_2_out), .eq(comparator_3_eq));  // open: gt, lt
  and and_3 (and_3_out, ~comparator_3_eq, and_2_out);  // AND_Gate
  nor nor_1 (ZERO, RESULT[31], RESULT[30], RESULT[29], RESULT[28], RESULT[27], RESULT[26], RESULT[25], RESULT[24], RESULT[23], RESULT[22], RESULT[21], RESULT[20], RESULT[19], RESULT[18], RESULT[17], RESULT[16], RESULT[15], RESULT[14], RESULT[13], RESULT[12], RESULT[11], RESULT[10], RESULT[9], RESULT[8], RESULT[7], RESULT[6], RESULT[5], RESULT[4], RESULT[3], RESULT[2], RESULT[1], RESULT[0]);
  or or_2 (OVF, and_3_out, and_5_out);
  and SUB (SUB_out, ~OP[2], ~OP[1], OP[0]);  // AND_Gate
  and and_4 (and_4_out, ~comparator_2_eq, SUB_out);  // AND_Gate
  and and_5 (and_5_out, comparator_3_eq, and_4_out);
  and ADD (ADD_out, ~OP[2], ~OP[1], ~OP[0]);  // AND_Gate

  // Other names for the same wires on the sheet: RES[31:0] = RESULT

  // Notes on the sheet:
  //   ULA - Unidade Lógica Aritmética
  //   ADD
  //   SUB
  //   AND
  //   OR
  //   SLL
  //   SRL
  //   SLT
endmodule

module BancoRegistradores (
  input  RW,
  input  [4:0] WR,
  input  CLK,
  input  [31:0] WD,
  input  [4:0] LR1,
  input  [4:0] LR2,
  output [31:0] LD1,
  output [31:0] LD2
);

  wire CLEAR, demultiplexer_1_out0, demultiplexer_1_out1, demultiplexer_1_out2, demultiplexer_1_out3,
       demultiplexer_1_out4, demultiplexer_1_out5, demultiplexer_1_out6, demultiplexer_1_out7,
       demultiplexer_1_out8, demultiplexer_1_out9, demultiplexer_1_out10, demultiplexer_1_out11,
       demultiplexer_1_out12, demultiplexer_1_out13, demultiplexer_1_out14, demultiplexer_1_out15,
       demultiplexer_1_out16, demultiplexer_1_out17, demultiplexer_1_out18, demultiplexer_1_out19,
       demultiplexer_1_out20, demultiplexer_1_out21, demultiplexer_1_out22, demultiplexer_1_out23,
       demultiplexer_1_out24, demultiplexer_1_out25, demultiplexer_1_out26, demultiplexer_1_out27,
       demultiplexer_1_out28, demultiplexer_1_out29, demultiplexer_1_out30, demultiplexer_1_out31;
  wire [31:0] R00000_q, R00001_q, R00010_q, R00011_q, R00100_q, R00101_q, R00110_q, R00111_q, R01000_q,
       R01001_q, R01010_q, R01011_q, R01100_q, R01101_q, R01110_q, R01111_q, R10000_q, R10001_q, R10010_q,
       R10011_q, R10100_q, R10101_q, R10110_q, R10111_q, R11000_q, R11001_q, R11010_q, R11011_q, R11100_q,
       R11101_q, R11110_q, R11111_q;

  Button u_CLEAR (.out(CLEAR));
  Register #(.width(32)) R00000 (.D(WD), .en(demultiplexer_1_out0), .Q(R00000_q), .clk(1'b0), .clr(CLEAR));
  Register #(.width(32)) R00001 (.D(WD), .en(demultiplexer_1_out1), .Q(R00001_q), .clk(CLK), .clr(CLEAR));
  Register #(.width(32)) R00010 (.D(WD), .en(demultiplexer_1_out2), .Q(R00010_q), .clk(CLK), .clr(CLEAR));
  Register #(.width(32)) R00011 (.D(WD), .en(demultiplexer_1_out3), .Q(R00011_q), .clk(CLK), .clr(CLEAR));
  Register #(.width(32)) R00100 (.D(WD), .en(demultiplexer_1_out4), .Q(R00100_q), .clk(CLK), .clr(CLEAR));
  Register #(.width(32)) R00101 (.D(WD), .en(demultiplexer_1_out5), .Q(R00101_q), .clk(CLK), .clr(CLEAR));
  Register #(.width(32)) R00110 (.D(WD), .en(demultiplexer_1_out6), .Q(R00110_q), .clk(CLK), .clr(CLEAR));
  Register #(.width(32)) R00111 (.D(WD), .en(demultiplexer_1_out7), .Q(R00111_q), .clk(CLK), .clr(CLEAR));
  Register #(.width(32)) R01000 (.D(WD), .en(demultiplexer_1_out8), .Q(R01000_q), .clk(CLK), .clr(CLEAR));
  Register #(.width(32)) R01001 (.D(WD), .en(demultiplexer_1_out9), .Q(R01001_q), .clk(CLK), .clr(CLEAR));
  Register #(.width(32)) R01010 (.D(WD), .en(demultiplexer_1_out10), .Q(R01010_q), .clk(CLK), .clr(CLEAR));
  Register #(.width(32)) R01011 (.D(WD), .en(demultiplexer_1_out11), .Q(R01011_q), .clk(CLK), .clr(CLEAR));
  Register #(.width(32)) R01100 (.D(WD), .en(demultiplexer_1_out12), .Q(R01100_q), .clk(CLK), .clr(CLEAR));
  Register #(.width(32)) R01101 (.D(WD), .en(demultiplexer_1_out13), .Q(R01101_q), .clk(CLK), .clr(CLEAR));
  Register #(.width(32)) R01110 (.D(WD), .en(demultiplexer_1_out14), .Q(R01110_q), .clk(CLK), .clr(CLEAR));
  Register #(.width(32)) R01111 (.D(WD), .en(demultiplexer_1_out15), .Q(R01111_q), .clk(CLK), .clr(CLEAR));
  Demultiplexer #(.select(5)) demultiplexer_1 (
    .out0(demultiplexer_1_out0), .out1(demultiplexer_1_out1), .out2(demultiplexer_1_out2),
    .out3(demultiplexer_1_out3), .out4(demultiplexer_1_out4), .out5(demultiplexer_1_out5),
    .out6(demultiplexer_1_out6), .out7(demultiplexer_1_out7), .out8(demultiplexer_1_out8),
    .out9(demultiplexer_1_out9), .out10(demultiplexer_1_out10), .out11(demultiplexer_1_out11),
    .out12(demultiplexer_1_out12), .out13(demultiplexer_1_out13), .out14(demultiplexer_1_out14),
    .out15(demultiplexer_1_out15), .out16(demultiplexer_1_out16), .out17(demultiplexer_1_out17),
    .out18(demultiplexer_1_out18), .out19(demultiplexer_1_out19), .out20(demultiplexer_1_out20),
    .out21(demultiplexer_1_out21), .out22(demultiplexer_1_out22), .out23(demultiplexer_1_out23),
    .out24(demultiplexer_1_out24), .out25(demultiplexer_1_out25), .out26(demultiplexer_1_out26),
    .out27(demultiplexer_1_out27), .out28(demultiplexer_1_out28), .out29(demultiplexer_1_out29),
    .out30(demultiplexer_1_out30), .out31(demultiplexer_1_out31), .in(RW), .sel(WR));  // open: en
  Register #(.width(32)) R10000 (.D(WD), .en(demultiplexer_1_out16), .Q(R10000_q), .clk(CLK), .clr(CLEAR));
  Register #(.width(32)) R10001 (.D(WD), .en(demultiplexer_1_out17), .Q(R10001_q), .clk(CLK), .clr(CLEAR));
  Register #(.width(32)) R10010 (.D(WD), .en(demultiplexer_1_out18), .Q(R10010_q), .clk(CLK), .clr(CLEAR));
  Register #(.width(32)) R10011 (.D(WD), .en(demultiplexer_1_out19), .Q(R10011_q), .clk(CLK), .clr(CLEAR));
  Register #(.width(32)) R10100 (.D(WD), .en(demultiplexer_1_out20), .Q(R10100_q), .clk(CLK), .clr(CLEAR));
  Register #(.width(32)) R10101 (.D(WD), .en(demultiplexer_1_out21), .Q(R10101_q), .clk(CLK), .clr(CLEAR));
  Register #(.width(32)) R10110 (.D(WD), .en(demultiplexer_1_out22), .Q(R10110_q), .clk(CLK), .clr(CLEAR));
  Register #(.width(32)) R10111 (.D(WD), .en(demultiplexer_1_out23), .Q(R10111_q), .clk(CLK), .clr(CLEAR));
  Register #(.width(32)) R11000 (.D(WD), .en(demultiplexer_1_out24), .Q(R11000_q), .clk(CLK), .clr(CLEAR));
  Register #(.width(32)) R11001 (.D(WD), .en(demultiplexer_1_out25), .Q(R11001_q), .clk(CLK), .clr(CLEAR));
  Register #(.width(32)) R11010 (.D(WD), .en(demultiplexer_1_out26), .Q(R11010_q), .clk(CLK), .clr(CLEAR));
  Register #(.width(32)) R11011 (.D(WD), .en(demultiplexer_1_out27), .Q(R11011_q), .clk(CLK), .clr(CLEAR));
  Register #(.width(32)) R11100 (.D(WD), .en(demultiplexer_1_out28), .Q(R11100_q), .clk(CLK), .clr(CLEAR));
  Register #(.width(32)) R11101 (.D(WD), .en(demultiplexer_1_out29), .Q(R11101_q), .clk(CLK), .clr(CLEAR));
  Register #(.width(32)) R11110 (.D(WD), .en(demultiplexer_1_out30), .Q(R11110_q), .clk(CLK), .clr(CLEAR));
  Register #(.width(32)) R11111 (.D(WD), .en(demultiplexer_1_out31), .Q(R11111_q), .clk(CLK), .clr(CLEAR));
  Multiplexer #(.select(5), .width(32)) multiplexer_1 (
    .in0(R00000_q), .in1(R00001_q), .in2(R00010_q), .in3(R00011_q), .in4(R00100_q), .in5(R00101_q),
    .in6(R00110_q), .in7(R00111_q), .in8(R01000_q), .in9(R01001_q), .in10(R01010_q), .in11(R01011_q),
    .in12(R01100_q), .in13(R01101_q), .in14(R01110_q), .in15(R01111_q), .in16(R10000_q), .in17(R10001_q),
    .in18(R10010_q), .in19(R10011_q), .in20(R10100_q), .in21(R10101_q), .in22(R10110_q), .in23(R10111_q),
    .in24(R11000_q), .in25(R11001_q), .in26(R11010_q), .in27(R11011_q), .in28(R11100_q), .in29(R11101_q),
    .in30(R11110_q), .in31(R11111_q), .out(LD2), .sel(LR2));  // open: en
  Multiplexer #(.select(5), .width(32)) multiplexer_2 (
    .in0(R00000_q), .in1(R00001_q), .in2(R00010_q), .in3(R00011_q), .in4(R00100_q), .in5(R00101_q),
    .in6(R00110_q), .in7(R00111_q), .in8(R01000_q), .in9(R01001_q), .in10(R01010_q), .in11(R01011_q),
    .in12(R01100_q), .in13(R01101_q), .in14(R01110_q), .in15(R01111_q), .in16(R10000_q), .in17(R10001_q),
    .in18(R10010_q), .in19(R10011_q), .in20(R10100_q), .in21(R10101_q), .in22(R10110_q), .in23(R10111_q),
    .in24(R11000_q), .in25(R11001_q), .in26(R11010_q), .in27(R11011_q), .in28(R11100_q), .in29(R11101_q),
    .in30(R11110_q), .in31(R11111_q), .out(LD1), .sel(LR1));  // open: en

  // Notes on the sheet:
  //   Banco de Registradores
endmodule

module Decodificador (
  input  [31:0] \Instrução ,
  output [25:0] ADDR,
  output [15:0] IMM,
  output [5:0] FUNCT,
  output [4:0] SHAMT,
  output [4:0] RD,
  output [4:0] RT,
  output [4:0] RS,
  output [5:0] OPCODE
);


  assign ADDR = \Instrução [25:0];
  assign FUNCT = \Instrução [5:0];
  assign IMM = \Instrução [15:0];
  assign OPCODE = \Instrução [31:26];
  assign RD = \Instrução [15:11];
  assign RS = \Instrução [25:21];
  assign RT = \Instrução [20:16];
  assign SHAMT = \Instrução [10:6];
endmodule

module ExtensorSinal (
  input  [15:0] IMM16,
  output [31:0] IMM32
);


  assign IMM32 = {{17{IMM16[15]}}, IMM16[14:0]};
endmodule

module MemoriaInstrucoes (
  input  [31:0] PCADDR,
  output [31:0] out_2
);

  ROM #(.addrWidth(19), .dataWidth(32)) rom_1 (.addr(PCADDR[20:2]), .data(out_2));  // open: sel

  // Notes on the sheet:
  //   contents of rom_1 (hex, n*v repeats v):
  //   20100002 20110007 9020 9820 22140001 12110002 2119022 810000a 2119020 810001a 211402a 11000002
  //   2109020 8100010 2319020 810001a 291402a 11000003 2749820 22940001 8100010 214402a 11000003 2749822
  //   2294ffff 8100015 20150014 aeb00000 8eb10000
endmodule

module MemoriaDados (
  input  MemWrite,
  input  [31:0] \Endereço ,
  input  CLK,
  input  MemRead,
  input  [31:0] EscreveDado,
  input  Clear,
  output [31:0] out_7
);

  RAM #(.addrWidth(24), .dataWidth(32), .bus("separate")) ram_1 (
    .addr(\Endereço [23:0]), .din(EscreveDado), .data(out_7), .str(MemWrite), .clk(CLK), .ld(MemRead),
    .clr(Clear));  // open: sel
endmodule

module UnidadeControle (
  input  [5:0] OP,
  output ALUSrc,
  output RegWrite,
  output RegDest,
  output MemToReg,
  output MemRead,
  output MemWrite,
  output Branch,
  output Jump,
  output [2:0] ALUOp
);

  wire addi, andi, ori, slti;

  and R (RegDest, ~OP[0], ~OP[1], ~OP[2], ~OP[3], ~OP[4], ~OP[5]);  // AND_Gate
  and u_addi (addi, ~OP[0], ~OP[1], ~OP[2], OP[3], ~OP[4], ~OP[5]);  // AND_Gate
  and u_andi (andi, ~OP[0], ~OP[1], OP[2], OP[3], ~OP[4], ~OP[5]);  // AND_Gate
  and u_ori (ori, OP[0], ~OP[1], OP[2], OP[3], ~OP[4], ~OP[5]);  // AND_Gate
  and u_slti (slti, ~OP[0], OP[1], ~OP[2], OP[3], ~OP[4], ~OP[5]);  // AND_Gate
  and lw (MemRead, OP[0], OP[1], ~OP[2], ~OP[3], ~OP[4], OP[5]);  // AND_Gate
  and sw (MemWrite, OP[0], OP[1], ~OP[2], OP[3], ~OP[4], OP[5]);  // AND_Gate
  and beq (Branch, ~OP[0], ~OP[1], OP[2], ~OP[3], ~OP[4], ~OP[5]);  // AND_Gate
  and j (Jump, ~OP[0], OP[1], ~OP[2], ~OP[3], ~OP[4], ~OP[5]);  // AND_Gate
  or or_1 (ALUSrc, addi, andi, ori, slti, MemRead, MemWrite);
  or or_2 (RegWrite, RegDest, addi, andi, ori, slti, MemRead);
  or or_3 (ALUOp[0], addi, MemRead, MemWrite, ori, Branch);
  or or_4 (ALUOp[1], andi, ori);
  or or_5 (ALUOp[2], slti, Branch);

  assign MemToReg = MemRead;

  // Other names for the same wires on the sheet: beq = Branch; lw = MemRead; sw = MemWrite

  // Notes on the sheet:
  //   ALUOp
  //   000
  //   001
  //   010
  //   011
  //   100
  //   101
  //   Operação
  //   R
  //   SOMA
  //   AND
  //   OR
  //   SLT
  //   SUB
  //   Instruções
  //   addi, lw, sw
  //   andi
  //   ori
  //   slti
  //   beq
endmodule

module ControleULA (
  input  [5:0] FUNCT,
  input  [2:0] ALUOp,
  output [2:0] OpULA
);

  wire addI, addR, andI, andR, orI, orR, R_out, sllR, sltI, sltR, srlR, subI, subR;

  and R (R_out, ~ALUOp[0], ~ALUOp[1], ~ALUOp[2]);  // AND_Gate
  and u_addI (addI, ALUOp[0], ~ALUOp[1], ~ALUOp[2]);  // AND_Gate
  and u_andI (andI, ~ALUOp[0], ALUOp[1], ~ALUOp[2]);  // AND_Gate
  and u_orI (orI, ALUOp[0], ALUOp[1], ~ALUOp[2]);  // AND_Gate
  and u_sltI (sltI, ~ALUOp[0], ~ALUOp[1], ALUOp[2]);  // AND_Gate
  and u_subI (subI, ALUOp[0], ~ALUOp[1], ALUOp[2]);  // AND_Gate
  and u_addR (addR, R_out, ~FUNCT[0], ~FUNCT[1], ~FUNCT[2], ~FUNCT[3], ~FUNCT[4], FUNCT[5]);  // AND_Gate
  and u_subR (subR, R_out, ~FUNCT[0], FUNCT[1], ~FUNCT[2], ~FUNCT[3], ~FUNCT[4], FUNCT[5]);  // AND_Gate
  and u_andR (andR, R_out, ~FUNCT[1], ~FUNCT[1], FUNCT[2], ~FUNCT[3], ~FUNCT[4], FUNCT[5]);  // AND_Gate
  and u_orR (orR, R_out, FUNCT[0], ~FUNCT[1], FUNCT[2], ~FUNCT[3], ~FUNCT[4], FUNCT[5]);  // AND_Gate
  and u_sllR (sllR, R_out, ~FUNCT[0], ~FUNCT[1], ~FUNCT[2], ~FUNCT[3], ~FUNCT[4], ~FUNCT[5]);  // AND_Gate
  and u_srlR (srlR, R_out, ~FUNCT[0], FUNCT[1], ~FUNCT[2], ~FUNCT[3], ~FUNCT[4], ~FUNCT[5]);  // AND_Gate
  and u_sltR (sltR, R_out, ~FUNCT[0], FUNCT[1], ~FUNCT[2], FUNCT[3], ~FUNCT[4], FUNCT[5]);  // AND_Gate
  or or_1 (OpULA[0], subR, subI, orR, orI, srlR);
  or or_2 (OpULA[1], andR, andI, orR, orI, sltR, sltI);
  or or_3 (OpULA[2], sllR, srlR, sltR, sltI);
endmodule

module _2conc (
  input  [25:0] Addr26,
  input  [31:0] Pc___4,
  output [31:0] out_3
);

  Shifter #(.width(28)) shifter_1 (.in({2'b00, Addr26}), .\dist (5'b00010), .out(out_3[27:0]));

  assign out_3[31:28] = Pc___4[31:28];
endmodule

module _2 (
  input  [31:0] in_1,
  output [31:0] out_2
);

  Shifter #(.width(32)) shifter_1 (.in(in_1), .\dist (5'b00010), .out(out_2));
endmodule
