// Logisim project [T1] ULA (Beatriz Moggio, Isabela Barotto).circ as structural Verilog: 1 circuit, main circuit main
module main (
  input  [2:0] OP,
  input  [4:0] SHAMT,
  input  [31:0] A,
  input  [31:0] B,
  output ZERO,
  output OVF,
  output [31:0] RESULT
);

  wire ADD_out, and_2_out, and_3_out, and_4_out, and_5_out, bitselector_1_out, bitselector_2_out,
       bitselector_3_out, comparator_1_lt, comparator_2_eq, comparator_3_eq, SUB_out;
  wire [31:0] adder_1_out, and_1_out, bit_extender_1_out, or_1_out, shifter_1_out, shifter_2_out,
       subtractor_1_out;

  // Probe on A
  // Probe on B
  // Probe on RESULT
  Adder #(.width(32)) adder_1 (.a(A), .b(B), .out(adder_1_out));  // open: cin, cout
  Subtractor #(.width(32)) subtractor_1 (.a(A), .b(B), .out(subtractor_1_out));  // open: bin, bout
  assign and_1_out = A & B;  // AND_Gate and_1, 32 bits wide
  assign or_1_out = A | B;  // OR_Gate or_1, 32 bits wide
  Shifter #(.width(32)) shifter_1 (.in(A), .\dist (SHAMT), .out(shifter_1_out));
  Shifter #(.width(32), .shift("lr")) shifter_2 (.in(A), .\dist (SHAMT), .out(shifter_2_out));
  Comparator #(.width(32)) comparator_1 (.a(A), .b(B), .lt(comparator_1_lt));  // open: gt, eq
  assign bit_extender_1_out = {{31{1'b0}}, comparator_1_lt};  // Bit_Extender bit_extender_1
  Multiplexer #(.select(3), .width(32)) multiplexer_1 (
    .in0(adder_1_out), .in1(subtractor_1_out), .in2(and_1_out), .in3(or_1_out), .in4(shifter_1_out),
    .in5(shifter_2_out), .in6(bit_extender_1_out), .out(RESULT), .sel(OP));  // open: in7, en
  BitSelector #(.width(32)) bitselector_1 (.in(A), .out(bitselector_1_out), .sel({5{1'b1}}));
  BitSelector #(.width(32)) bitselector_2 (.in(B), .out(bitselector_2_out), .sel({5{1'b1}}));
  BitSelector #(.width(32)) bitselector_3 (.in(RESULT), .out(bitselector_3_out), .sel({5{1'b1}}));
  Comparator #(.width(1)) comparator_2 (
    .a(bitselector_1_out), .b(bitselector_2_out), .eq(comparator_2_eq));  // open: gt, lt
  and and_2 (and_2_out, comparator_2_eq, ADD_out);
  Comparator #(.width(1)) comparator_3 (
    .a(bitselector_3_out), .b(bitselector_2_out), .eq(comparator_3_eq));  // open: gt, lt
  and and_3 (and_3_out, ~comparator_3_eq, and_2_out);  // AND_Gate
  nor nor_1 (ZERO, RESULT[31], RESULT[30], RESULT[29], RESULT[28], RESULT[27], RESULT[26], RESULT[25], RESULT[24], RESULT[23], RESULT[22], RESULT[21], RESULT[20], RESULT[19], RESULT[18], RESULT[17], RESULT[16], RESULT[15], RESULT[14], RESULT[13], RESULT[12], RESULT[11], RESULT[10], RESULT[9], RESULT[8], RESULT[7], RESULT[6], RESULT[5], RESULT[4], RESULT[3], RESULT[2], RESULT[1], RESULT[0]);
  or or_2 (OVF, and_3_out, and_5_out);
  and SUB (SUB_out, ~OP[2], ~OP[1], OP[0]);  // AND_Gate
  and and_4 (and_4_out, ~comparator_2_eq, SUB_out);  // AND_Gate
  and and_5 (and_5_out, comparator_3_eq, and_4_out);
  and ADD (ADD_out, ~OP[2], ~OP[1], ~OP[0]);  // AND_Gate

  // Other names for the same wires on the sheet: RES[31:0] = RESULT

  // Notes on the sheet:
  //   ULA - Unidade Lógica Aritmética
  //   ADD
  //   SUB
  //   AND
  //   OR
  //   SLL
  //   SRL
  //   SLT
endmodule
