// Logisim project [T2] Banco de Registradores (Beatriz Moggio, Isabela Barotto).circ as structural Verilog: 1 circuit, main circuit main
module main (
  input  RW,
  input  [4:0] WR,
  input  [31:0] WD,
  input  [4:0] LR1,
  input  [4:0] LR2,
  output [31:0] LD1,
  output [31:0] LD2
);

  wire CLEAR, CLK, demultiplexer_1_out0, demultiplexer_1_out1, demultiplexer_1_out2, demultiplexer_1_out3,
       demultiplexer_1_out4, demultiplexer_1_out5, demultiplexer_1_out6, demultiplexer_1_out7,
       demultiplexer_1_out8, demultiplexer_1_out9, demultiplexer_1_out10, demultiplexer_1_out11,
       demultiplexer_1_out12, demultiplexer_1_out13, demultiplexer_1_out14, demultiplexer_1_out15,
       demultiplexer_1_out16, demultiplexer_1_out17, demultiplexer_1_out18, demultiplexer_1_out19,
       demultiplexer_1_out20, demultiplexer_1_out21, demultiplexer_1_out22, demultiplexer_1_out23,
       demultiplexer_1_out24, demultiplexer_1_out25, demultiplexer_1_out26, demultiplexer_1_out27,
       demultiplexer_1_out28, demultiplexer_1_out29, demultiplexer_1_out30, demultiplexer_1_out31;
  wire [31:0] R00000_q, R00001_q, R00010_q, R00011_q, R00100_q, R00101_q, R00110_q, R00111_q, R01000_q,
       R01001_q, R01010_q, R01011_q, R01100_q, R01101_q, R01110_q, R01111_q, R10000_q, R10001_q, R10010_q,
       R10011_q, R10100_q, R10101_q, R10110_q, R10111_q, R11000_q, R11001_q, R11010_q, R11011_q, R11100_q,
       R11101_q, R11110_q, R11111_q;

  Clock u_CLK (.out(CLK));
  Button u_CLEAR (.out(CLEAR));
  Register #(.width(32)) R00000 (.D(WD), .en(demultiplexer_1_out0), .Q(R00000_q), .clk(1'b0), .clr(CLEAR));
  Register #(.width(32)) R00001 (.D(WD), .en(demultiplexer_1_out1), .Q(R00001_q), .clk(CLK), .clr(CLEAR));
  Register #(.width(32)) R00010 (.D(WD), .en(demultiplexer_1_out2), .Q(R00010_q), .clk(CLK), .clr(CLEAR));
  Register #(.width(32)) R00011 (.D(WD), .en(demultiplexer_1_out3), .Q(R00011_q), .clk(CLK), .clr(CLEAR));
  Register #(.width(32)) R00100 (.D(WD), .en(demultiplexer_1_out4), .Q(R00100_q), .clk(CLK), .clr(CLEAR));
  Register #(.width(32)) R00101 (.D(WD), .en(demultiplexer_1_out5), .Q(R00101_q), .clk(CLK), .clr(CLEAR));
  Register #(.width(32)) R00110 (.D(WD), .en(demultiplexer_1_out6), .Q(R00110_q), .clk(CLK), .clr(CLEAR));
  Register #(.width(32)) R00111 (.D(WD), .en(demultiplexer_1_out7), .Q(R00111_q), .clk(CLK), .clr(CLEAR));
  Register #(.width(32)) R01000 (.D(WD), .en(demultiplexer_1_out8), .Q(R01000_q), .clk(CLK), .clr(CLEAR));
  Register #(.width(32)) R01001 (.D(WD), .en(demultiplexer_1_out9), .Q(R01001_q), .clk(CLK), .clr(CLEAR));
  Register #(.width(32)) R01010 (.D(WD), .en(demultiplexer_1_out10), .Q(R01010_q), .clk(CLK), .clr(CLEAR));
  Register #(.width(32)) R01011 (.D(WD), .en(demultiplexer_1_out11), .Q(R01011_q), .clk(CLK), .clr(CLEAR));
  Register #(.width(32)) R01100 (.D(WD), .en(demultiplexer_1_out12), .Q(R01100_q), .clk(CLK), .clr(CLEAR));
  Register #(.width(32)) R01101 (.D(WD), .en(demultiplexer_1_out13), .Q(R01101_q), .clk(CLK), .clr(CLEAR));
  Register #(.width(32)) R01110 (.D(WD), .en(demultiplexer_1_out14), .Q(R01110_q), .clk(CLK), .clr(CLEAR));
  Register #(.width(32)) R01111 (.D(WD), .en(demultiplexer_1_out15), .Q(R01111_q), .clk(CLK), .clr(CLEAR));
  Demultiplexer #(.select(5)) demultiplexer_1 (
    .out0(demultiplexer_1_out0), .out1(demultiplexer_1_out1), .out2(demultiplexer_1_out2),
    .out3(demultiplexer_1_out3), .out4(demultiplexer_1_out4), .out5(demultiplexer_1_out5),
    .out6(demultiplexer_1_out6), .out7(demultiplexer_1_out7), .out8(demultiplexer_1_out8),
    .out9(demultiplexer_1_out9), .out10(demultiplexer_1_out10), .out11(demultiplexer_1_out11),
    .out12(demultiplexer_1_out12), .out13(demultiplexer_1_out13), .out14(demultiplexer_1_out14),
    .out15(demultiplexer_1_out15), .out16(demultiplexer_1_out16), .out17(demultiplexer_1_out17),
    .out18(demultiplexer_1_out18), .out19(demultiplexer_1_out19), .out20(demultiplexer_1_out20),
    .out21(demultiplexer_1_out21), .out22(demultiplexer_1_out22), .out23(demultiplexer_1_out23),
    .out24(demultiplexer_1_out24), .out25(demultiplexer_1_out25), .out26(demultiplexer_1_out26),
    .out27(demultiplexer_1_out27), .out28(demultiplexer_1_out28), .out29(demultiplexer_1_out29),
    .out30(demultiplexer_1_out30), .out31(demultiplexer_1_out31), .in(RW), .sel(WR));  // open: en
  Register #(.width(32)) R10000 (.D(WD), .en(demultiplexer_1_out16), .Q(R10000_q), .clk(CLK), .clr(CLEAR));
  Register #(.width(32)) R10001 (.D(WD), .en(demultiplexer_1_out17), .Q(R10001_q), .clk(CLK), .clr(CLEAR));
  Register #(.width(32)) R10010 (.D(WD), .en(demultiplexer_1_out18), .Q(R10010_q), .clk(CLK), .clr(CLEAR));
  Register #(.width(32)) R10011 (.D(WD), .en(demultiplexer_1_out19), .Q(R10011_q), .clk(CLK), .clr(CLEAR));
  Register #(.width(32)) R10100 (.D(WD), .en(demultiplexer_1_out20), .Q(R10100_q), .clk(CLK), .clr(CLEAR));
  Register #(.width(32)) R10101 (.D(WD), .en(demultiplexer_1_out21), .Q(R10101_q), .clk(CLK), .clr(CLEAR));
  Register #(.width(32)) R10110 (.D(WD), .en(demultiplexer_1_out22), .Q(R10110_q), .clk(CLK), .clr(CLEAR));
  Register #(.width(32)) R10111 (.D(WD), .en(demultiplexer_1_out23), .Q(R10111_q), .clk(CLK), .clr(CLEAR));
  Register #(.width(32)) R11000 (.D(WD), .en(demultiplexer_1_out24), .Q(R11000_q), .clk(CLK), .clr(CLEAR));
  Register #(.width(32)) R11001 (.D(WD), .en(demultiplexer_1_out25), .Q(R11001_q), .clk(CLK), .clr(CLEAR));
  Register #(.width(32)) R11010 (.D(WD), .en(demultiplexer_1_out26), .Q(R11010_q), .clk(CLK), .clr(CLEAR));
  Register #(.width(32)) R11011 (.D(WD), .en(demultiplexer_1_out27), .Q(R11011_q), .clk(CLK), .clr(CLEAR));
  Register #(.width(32)) R11100 (.D(WD), .en(demultiplexer_1_out28), .Q(R11100_q), .clk(CLK), .clr(CLEAR));
  Register #(.width(32)) R11101 (.D(WD), .en(demultiplexer_1_out29), .Q(R11101_q), .clk(CLK), .clr(CLEAR));
  Register #(.width(32)) R11110 (.D(WD), .en(demultiplexer_1_out30), .Q(R11110_q), .clk(CLK), .clr(CLEAR));
  Register #(.width(32)) R11111 (.D(WD), .en(demultiplexer_1_out31), .Q(R11111_q), .clk(CLK), .clr(CLEAR));
  Multiplexer #(.select(5), .width(32)) multiplexer_1 (
    .in0(R00000_q), .in1(R00001_q), .in2(R00010_q), .in3(R00011_q), .in4(R00100_q), .in5(R00101_q),
    .in6(R00110_q), .in7(R00111_q), .in8(R01000_q), .in9(R01001_q), .in10(R01010_q), .in11(R01011_q),
    .in12(R01100_q), .in13(R01101_q), .in14(R01110_q), .in15(R01111_q), .in16(R10000_q), .in17(R10001_q),
    .in18(R10010_q), .in19(R10011_q), .in20(R10100_q), .in21(R10101_q), .in22(R10110_q), .in23(R10111_q),
    .in24(R11000_q), .in25(R11001_q), .in26(R11010_q), .in27(R11011_q), .in28(R11100_q), .in29(R11101_q),
    .in30(R11110_q), .in31(R11111_q), .out(LD2), .sel(LR2));  // open: en
  Multiplexer #(.select(5), .width(32)) multiplexer_2 (
    .in0(R00000_q), .in1(R00001_q), .in2(R00010_q), .in3(R00011_q), .in4(R00100_q), .in5(R00101_q),
    .in6(R00110_q), .in7(R00111_q), .in8(R01000_q), .in9(R01001_q), .in10(R01010_q), .in11(R01011_q),
    .in12(R01100_q), .in13(R01101_q), .in14(R01110_q), .in15(R01111_q), .in16(R10000_q), .in17(R10001_q),
    .in18(R10010_q), .in19(R10011_q), .in20(R10100_q), .in21(R10101_q), .in22(R10110_q), .in23(R10111_q),
    .in24(R11000_q), .in25(R11001_q), .in26(R11010_q), .in27(R11011_q), .in28(R11100_q), .in29(R11101_q),
    .in30(R11110_q), .in31(R11111_q), .out(LD1), .sel(LR1));  // open: en

  // Notes on the sheet:
  //   Banco de Registradores
endmodule
